// Logisim project CRC.circ as structural Verilog: 3 circuits, main circuit CRC
module CRC (
  input  [7:0] in_1,
  input  [3:0] in_2,
  output [10:0] out_3
);

  wire [2:0] \四位除法_1_余数 , \四位除法_2_余数 , \四位除法_3_余数 , \四位除法_4_余数 , \四位除法_5_余数 , \四位除法_6_余数 , \四位除法_7_余数 ;

  \四位除法  \u_四位除法_1  (.\被除数 (in_1[7:4]), .\除数 (in_2), .\余数 (\四位除法_1_余数 ));
  \四位除法  \u_四位除法_2  (.\被除数 ({\四位除法_1_余数 , in_1[3]}), .\除数 (in_2), .\余数 (\四位除法_2_余数 ));
  \四位除法  \u_四位除法_3  (.\被除数 ({\四位除法_2_余数 , in_1[2]}), .\除数 (in_2), .\余数 (\四位除法_3_余数 ));
  \四位除法  \u_四位除法_4  (.\被除数 ({\四位除法_3_余数 , in_1[1]}), .\除数 (in_2), .\余数 (\四位除法_4_余数 ));
  \四位除法  \u_四位除法_5  (.\被除数 ({\四位除法_4_余数 , in_1[0]}), .\除数 (in_2), .\余数 (\四位除法_5_余数 ));
  \四位除法  \u_四位除法_6  (.\被除数 ({\四位除法_5_余数 , 1'b0}), .\除数 (in_2), .\余数 (\四位除法_6_余数 ));
  \四位除法  \u_四位除法_7  (.\被除数 ({\四位除法_6_余数 , 1'b0}), .\除数 (in_2), .\余数 (\四位除法_7_余数 ));
  \四位除法  \u_四位除法_8  (.\被除数 ({\四位除法_7_余数 , 1'b0}), .\除数 (in_2), .\余数 (out_3[2:0]));

  assign out_3[10:3] = in_1;

  // Other names for the same wires on the sheet: 除数[3:0] = in_2
endmodule

module \四位除法  (
  input  [3:0] \被除数 ,
  input  [3:0] \除数 ,
  output [2:0] \余数 
);

  wire bit_extender_2_out;
  wire [2:0] bit_extender_1_out, bit_extender_3_out;
  wire [3:0] shifter_1_out, xor_1_out;

  assign xor_1_out = \被除数  ^ \除数 ;  // XOR_Gate xor_1, 4 bits wide
  Bit_Extender #(.in_width(4), .out_width(3)) bit_extender_1 (.in(\被除数 ), .out(bit_extender_1_out));
  Shifter #(.width(4), .shift("lr")) shifter_1 (.in(\被除数 ), .\dist (2'b11), .out(shifter_1_out));
  Bit_Extender #(.in_width(4), .out_width(1)) bit_extender_2 (.in(shifter_1_out), .out(bit_extender_2_out));
  Bit_Extender #(.in_width(4), .out_width(3)) bit_extender_3 (.in(xor_1_out), .out(bit_extender_3_out));
  Multiplexer #(.width(3)) multiplexer_1 (
    .in0(bit_extender_1_out), .in1(bit_extender_3_out), .out(\余数 ), .sel(bit_extender_2_out));  // open: en
endmodule

module Draft (
);

  wire [0:0] undriven;
  wire [2:0] undriven_2;
  wire [3:0] \除数 ;

  \四位除法  \u_四位除法_1  (.\被除数 ({undriven_2, undriven[0]}), .\除数 (\除数 ));  // open: 余数
endmodule
