// Logisim project fsm.circ as structural Verilog: 4 circuits, main circuit fsm
module fsm (
  input  in_1,
  input  [1:0] in_2,
  output out_3
);

  wire statestoration_1_out_4, statestoration_1_out_5, statetrans_1_x, statetrans_1_y;

  StateTrans statetrans_1 (
    .a(statestoration_1_out_4), .b(statestoration_1_out_5), .c(in_2[1]), .d(in_2[0]), .x(statetrans_1_x),
    .y(statetrans_1_y));
  StateStoration statestoration_1 (
    .in_1(statetrans_1_x), .in_2(statetrans_1_y), .in_3(in_1), .out_4(statestoration_1_out_4),
    .out_5(statestoration_1_out_5));
  StateOutput stateoutput_1 (
    .a(statestoration_1_out_4), .b(statestoration_1_out_5), .c(in_2[1]), .d(in_2[0]), .x(out_3));
endmodule

module StateTrans (
  input  a,
  input  b,
  input  c,
  input  d,
  output x,
  output y
);

  wire and_1_out, and_2_out, and_3_out, and_4_out, not_1_out, not_2_out, not_3_out, not_4_out, not_5_out,
       not_6_out, not_7_out;

  not not_1 (not_1_out, a);
  and and_1 (and_1_out, not_1_out, b, not_2_out);
  not not_2 (not_2_out, d);
  and and_2 (and_2_out, a, not_3_out, not_4_out);
  not not_3 (not_3_out, b);
  not not_4 (not_4_out, d);
  not not_5 (not_5_out, c);
  and and_3 (and_3_out, not_5_out, d);
  not not_6 (not_6_out, b);
  and and_4 (and_4_out, a, not_6_out, not_7_out);
  not not_7 (not_7_out, d);
  or or_1 (x, and_1_out, and_2_out);
  or or_2 (y, and_3_out, and_4_out);
endmodule

module StateOutput (
  input  a,
  input  b,
  input  c,
  input  d,
  output x
);

  wire not_1_out, not_2_out;

  not not_1 (not_1_out, b);
  and and_1 (x, a, not_1_out, not_2_out);
  not not_2 (not_2_out, d);
endmodule

module StateStoration (
  input  in_1,
  input  in_2,
  input  in_3,
  output out_4,
  output out_5
);

  wire clk, multiplexer_1_out, multiplexer_2_out;

  Clock clock_1 (.out(clk));
  Multiplexer multiplexer_1 (.in0(in_1), .in1(1'b0), .out(multiplexer_1_out), .sel(in_3));  // open: en
  Register #(.width(1)) register_1 (.D(multiplexer_1_out), .Q(out_4), .clk(clk));  // open: en, clr
  Multiplexer multiplexer_2 (.in0(in_2), .in1(1'b0), .out(multiplexer_2_out), .sel(in_3));  // open: en
  Register #(.width(1)) register_2 (.D(multiplexer_2_out), .Q(out_5), .clk(clk));  // open: en, clr

  // Other names for the same wires on the sheet: clr = in_3
endmodule
