// Logisim project ftoi.circ as structural Verilog: 3 circuits, main circuit ftoi
module ftoi (
  input  [15:0] in_1,
  output [31:0] out_2
);

  wire Denormalized, NaN_Inf, Normalized, not_1_out, not_2_out;
  wire [31:0] bit_extender_1_out, getint_1_out_3, shift_1_out_3, temp;

  Comparator #(.width(5)) comparator_1 (.a(in_1[14:10]), .b({5{1'b1}}), .eq(NaN_Inf));  // open: gt, lt
  Comparator #(.width(5)) comparator_2 (.a(in_1[14:10]), .b({5{1'b0}}), .eq(Denormalized));  // open: gt, lt
  not not_1 (not_1_out, Denormalized);
  and and_1 (Normalized, not_1_out, not_2_out);
  not not_2 (not_2_out, NaN_Inf);
  // Probe on in_1[14:10]
  // Probe on {1'b0, Normalized, in_1[9:0]}
  assign bit_extender_1_out = {{20{1'b0}}, {1'b0, Normalized, in_1[9:0]}};  // Bit_Extender bit_extender_1
  // Probe on bit_extender_1_out
  // Probe on getint_1_out_3
  getInt getint_1 (.in_1(temp), .in_2(in_1[15]), .out_3(getint_1_out_3));
  // Probe on shift_1_out_3
  shift shift_1 (.in_1(in_1[14:10]), .in_2(bit_extender_1_out), .out_3(shift_1_out_3));
  Multiplexer #(.width(32)) multiplexer_1 (
    .in0(getint_1_out_3), .in1({32{1'b0}}), .out(out_2), .sel(NaN_Inf));  // open: en
  // Probe on temp
  Shifter #(.width(32), .shift("lr")) shifter_1 (.in(shift_1_out_3), .\dist (5'b01010), .out(temp));

  // Other names for the same wires on the sheet: fraction[9:0] = in_1[9:0]; exp[4:0] = in_1[14:10]; s = in_1[15]
endmodule

module shift (
  input  [4:0] in_1,
  input  [31:0] in_2,
  output [31:0] out_3
);

  wire negative, positive;
  wire [4:0] E, subtractor_1_out, subtractor_2_out;
  wire [31:0] shifter_1_out, shifter_2_out;

  Comparator #(.width(5), .mode("unsigned")) comparator_1 (
    .a(in_1), .b(5'b01111), .gt(positive), .lt(negative));  // open: eq
  Subtractor #(.width(5)) subtractor_1 (.a(in_1), .b(5'b01111), .out(subtractor_1_out));  // open: bin, bout
  Subtractor #(.width(5)) subtractor_2 (.a(5'b01111), .b(in_1), .out(subtractor_2_out));  // open: bin, bout
  Shifter #(.width(32)) shifter_1 (.in(in_2), .\dist (E), .out(shifter_1_out));
  Shifter #(.width(32), .shift("lr")) shifter_2 (.in(in_2), .\dist (E), .out(shifter_2_out));
  Multiplexer #(.width(5)) multiplexer_1 (
    .in0(subtractor_1_out), .in1(subtractor_2_out), .out(E), .sel(negative));  // open: en
  Multiplexer #(.width(32)) multiplexer_2 (
    .in0(shifter_1_out), .in1(shifter_2_out), .out(out_3), .sel(negative));  // open: en

  // Other names for the same wires on the sheet: exp[4:0] = in_1; input[31:0] = in_2

  // Notes on the sheet:
  //   根据E的正负决定左移还是右移
endmodule

module getInt (
  input  [31:0] in_1,
  input  in_2,
  output [31:0] out_3
);

  wire [31:0] negator_1_out;

  Negator #(.width(32)) negator_1 (.in(in_1), .out(negator_1_out));
  Multiplexer #(.width(32)) multiplexer_1 (.in0(in_1), .in1(negator_1_out), .out(out_3), .sel(in_2));  // open: en

  // Other names for the same wires on the sheet: input[31:0] = in_1; s = in_2
endmodule
