// Logisim project navigation.circ as structural Verilog: 3 circuits, main circuit navigation
module navigation (
  input  [1:0] in_1,
  input  in_2,
  input  in_3,
  output out_4,
  output out_5
);

  wire statetrans_1_u, statetrans_1_x, statetrans_1_y, statetrans_1_z;
  wire [2:0] statestore_1_out_9;

  StateTrans statetrans_1 (
    .a(statestore_1_out_9[2]), .b(statestore_1_out_9[1]), .c(statestore_1_out_9[0]), .d(in_1[1]),
    .e(in_1[0]), .x(statetrans_1_x), .y(statetrans_1_y), .z(statetrans_1_z), .u(statetrans_1_u));
  StateStore statestore_1 (
    .in_1(statetrans_1_x), .in_2(statetrans_1_y), .in_3(statetrans_1_z), .in_4(statetrans_1_u), .in_5(in_2),
    .in_6(in_3), .out_7(statestore_1_out_9[2]), .out_8(statestore_1_out_9[1]), .out_9(statestore_1_out_9[0]),
    .out_10(out_5));
  Comparator #(.width(3)) comparator_1 (.a(statestore_1_out_9), .b(3'b100), .eq(out_4));  // open: gt, lt
endmodule

module StateTrans (
  input  a,
  input  b,
  input  c,
  input  d,
  input  e,
  output x,
  output y,
  output z,
  output u
);

  wire and_1_out, and_2_out, and_3_out, and_4_out, and_5_out, and_6_out, and_7_out, and_8_out, and_9_out,
       and_10_out, and_11_out, and_12_out, and_13_out, and_14_out, and_15_out, and_16_out, not_1_out,
       not_2_out, not_3_out, not_4_out, not_5_out, not_6_out, not_7_out, not_8_out, not_9_out, not_10_out,
       not_11_out, not_12_out, not_13_out, not_14_out, not_15_out, not_16_out, not_17_out, not_18_out,
       not_19_out, not_20_out, not_21_out, not_22_out, not_23_out, not_24_out, not_25_out, not_26_out,
       not_27_out, not_28_out;

  not not_1 (not_1_out, c);
  not not_2 (not_2_out, d);
  not not_3 (not_3_out, e);
  not not_4 (not_4_out, d);
  not not_5 (not_5_out, b);
  not not_6 (not_6_out, d);
  not not_7 (not_7_out, d);
  not not_8 (not_8_out, e);
  not not_9 (not_9_out, c);
  not not_10 (not_10_out, d);
  not not_11 (not_11_out, c);
  not not_12 (not_12_out, e);
  not not_13 (not_13_out, a);
  not not_14 (not_14_out, b);
  not not_15 (not_15_out, d);
  not not_16 (not_16_out, e);
  not not_17 (not_17_out, e);
  not not_18 (not_18_out, a);
  not not_19 (not_19_out, c);
  not not_20 (not_20_out, d);
  not not_21 (not_21_out, a);
  not not_22 (not_22_out, b);
  not not_23 (not_23_out, c);
  not not_24 (not_24_out, a);
  not not_25 (not_25_out, c);
  not not_26 (not_26_out, e);
  not not_27 (not_27_out, d);
  not not_28 (not_28_out, e);
  and and_1 (and_1_out, b, not_1_out, not_2_out, not_3_out);
  and and_2 (and_2_out, b, c, not_4_out, e);
  and and_3 (and_3_out, not_5_out, c, not_6_out);
  and and_4 (and_4_out, c, not_7_out, not_8_out);
  and and_5 (and_5_out, b, not_9_out, not_10_out, e);
  and and_6 (and_6_out, b, not_11_out, d, not_12_out);
  and and_7 (and_7_out, b, c, d, e);
  and and_8 (and_8_out, not_13_out, not_14_out, not_15_out, not_16_out);
  and and_9 (and_9_out, c, d, e);
  and and_10 (and_10_out, b, d, e);
  and and_11 (and_11_out, b, c, not_17_out);
  and and_12 (and_12_out, not_18_out, not_19_out, not_20_out, e);
  and and_13 (and_13_out, not_21_out, not_22_out, not_23_out, d);
  and and_14 (and_14_out, not_24_out, not_25_out, d, not_26_out);
  and and_15 (and_15_out, c, d, e);
  and and_16 (and_16_out, b, c, not_27_out, not_28_out);
  or or_1 (x, and_1_out, and_2_out);
  or or_2 (y, and_3_out, and_4_out, and_5_out, and_6_out, and_7_out);
  or or_3 (z, and_8_out, and_9_out, and_10_out, and_11_out);
  or or_4 (u, and_12_out, and_13_out, and_14_out, and_15_out, and_16_out);
endmodule

module StateStore (
  input  in_1,
  input  in_2,
  input  in_3,
  input  in_4,
  input  in_5,
  input  in_6,
  output out_7,
  output out_8,
  output out_9,
  output out_10
);

  Register #(.width(1)) register_1 (.D(in_1), .Q(out_7), .clk(in_5), .clr(in_6));  // open: en
  Register #(.width(1)) register_2 (.D(in_2), .Q(out_8), .clk(in_5), .clr(in_6));  // open: en
  Register #(.width(1)) register_3 (.D(in_3), .Q(out_9), .clk(in_5), .clr(in_6));  // open: en
  Register #(.width(1)) register_4 (.D(in_4), .Q(out_10), .clk(in_5), .clr(in_6));  // open: en

  // Other names for the same wires on the sheet: clk = in_5; rst = in_6
endmodule
