// Logisim project ftoi_down_trun.circ as structural Verilog: 3 circuits, main circuit ftoi
module ftoi (
  input  [15:0] in_1,
  output [31:0] out_2
);

  wire comparator_4_eq, Denormalized, isInt, low10bits, NaN_Inf, Normalized, not_1_out, not_2_out;
  wire [4:0] E;
  wire [31:0] bit_extender_1_out, DOutput, getint_1_out_4, NOutput, shift_1_out_3, temp;

  Comparator #(.width(5)) comparator_1 (.a(in_1[14:10]), .b({5{1'b1}}), .eq(NaN_Inf));  // open: gt, lt
  Comparator #(.width(5)) comparator_2 (.a(in_1[14:10]), .b({5{1'b0}}), .eq(Denormalized));  // open: gt, lt
  not not_1 (not_1_out, Denormalized);
  and and_1 (Normalized, not_1_out, not_2_out);
  not not_2 (not_2_out, NaN_Inf);
  Subtractor #(.width(5)) subtractor_1 (.a(in_1[14:10]), .b(5'b01111), .out(E));  // open: bin, bout
  // Probe on E
  // Probe on {1'b0, Normalized, in_1[9:0]}
  assign bit_extender_1_out = {{20{1'b0}}, {1'b0, Normalized, in_1[9:0]}};  // Bit_Extender bit_extender_1
  getInt getint_1 (.in_1(temp), .in_2(in_1[15]), .in_3(isInt), .out_4(getint_1_out_4));
  Multiplexer #(.width(32)) multiplexer_1 (.in0(NOutput), .in1(DOutput), .sel(Denormalized));  // open: out, en
  // Probe on shift_1_out_3
  shift shift_1 (.in_1(E), .in_2(bit_extender_1_out), .out_3(shift_1_out_3));
  // Probe on getint_1_out_4
  // Probe on temp
  Shifter #(.width(32), .shift("ar")) shifter_1 (.in(shift_1_out_3), .\dist (5'b01010), .out(temp));
  Comparator #(.width(10)) comparator_3 (.a(shift_1_out_3[9:0]), .b({10{1'b0}}), .eq(low10bits));  // open: gt, lt
  Comparator #(.width(10)) comparator_4 (.a(in_1[9:0]), .b({10{1'b0}}), .eq(comparator_4_eq));  // open: gt, lt
  Multiplexer #(.width(32)) multiplexer_2 (
    .in0(getint_1_out_4), .in1({32{1'b0}}), .out(out_2), .sel(NaN_Inf));  // open: en
  and and_2 (isInt, low10bits, comparator_4_eq);

  // Other names for the same wires on the sheet: fraction[9:0] = in_1[9:0]; exp[4:0] = in_1[14:10]; s = in_1[15]
endmodule

module shift (
  input  [4:0] in_1,
  input  [31:0] in_2,
  output [31:0] out_3
);

  wire negative;
  wire [3:0] and_1_out;
  wire [4:0] negator_1_out;
  wire [31:0] shifter_1_out, shifter_2_out;

  assign {negative, and_1_out} = in_1 & 5'b10000;  // AND_Gate and_1, 5 bits wide
  Negator #(.width(5)) negator_1 (.in(in_1), .out(negator_1_out));
  // Probe on negator_1_out
  Shifter #(.width(32)) shifter_1 (.in(in_2), .\dist (in_1), .out(shifter_1_out));
  Shifter #(.width(32), .shift("ar")) shifter_2 (.in(in_2), .\dist (negator_1_out), .out(shifter_2_out));
  Multiplexer #(.width(32)) multiplexer_1 (
    .in0(shifter_1_out), .in1(shifter_2_out), .out(out_3), .sel(negative));  // open: en

  // Other names for the same wires on the sheet: E[4:0] = in_1; input[31:0] = in_2

  // Notes on the sheet:
  //   根据E的正负决定左移还是右移
endmodule

module getInt (
  input  [31:0] in_1,
  input  in_2,
  input  in_3,
  output [31:0] out_4
);

  wire not_1_out, sel;
  wire [31:0] negator_1_out, subtractor_1_out;

  not not_1 (not_1_out, in_3);
  Negator #(.width(32)) negator_1 (.in(in_1), .out(negator_1_out));
  and and_1 (sel, in_2, not_1_out);
  Subtractor #(.width(32)) subtractor_1 (.a(negator_1_out), .b(32'h1), .out(subtractor_1_out));  // open: bin, bout
  Multiplexer #(.width(32)) multiplexer_1 (.in0(in_1), .in1(subtractor_1_out), .out(out_4), .sel(sel));  // open: en

  // Other names for the same wires on the sheet: input[31:0] = in_1; isInt = in_3; s = in_2
endmodule
