// Logisim project navigation ori.circ as structural Verilog
module navigation (
  input  [1:0] dir,
  input  clk,
  input  reset,
  output arrive,
  output hit
);

  wire counter_1_q, counter_2_q, counter_3_q, in0, in1, in2, register_1_q, register_2_q, register_3_q,
       \状态转移_1_c02 , \状态转移_1_c12 , \状态转移_1_c22 , \状态转移_1_hit ;

  \状态转移  \u_状态转移_1  (
    .C2(in2), .C1(in1), .C0(in0), .D1(dir[1]), .D0(dir[0]), .C22(\状态转移_1_c22 ), .C12(\状态转移_1_c12 ),
    .C02(\状态转移_1_c02 ), .hit(\状态转移_1_hit ), .arrive(arrive));
  Register #(.width(1)) register_1 (.D(\状态转移_1_c22 ), .Q(register_1_q), .clk(clk), .clr(reset));  // open: en
  Register #(.width(1)) register_2 (.D(\状态转移_1_c12 ), .Q(register_2_q), .clk(clk), .clr(reset));  // open: en
  Register #(.width(1)) register_3 (.D(\状态转移_1_c02 ), .Q(register_3_q), .clk(clk), .clr(reset));  // open: en
  Register #(.width(1)) register_4 (.D(\状态转移_1_hit ), .Q(hit), .clk(clk), .clr(reset));  // open: en
  Multiplexer multiplexer_1 (.in0(1'b0), .in1(register_1_q), .out(in2), .sel(counter_1_q));  // open: en
  Counter #(.width(1), .max('h1), .ongoal("stay")) counter_1 (
    .Q(counter_1_q), .clk(clk), .clr(reset));  // open: load, D, count, carry
  Multiplexer multiplexer_2 (.in0(1'b0), .in1(register_2_q), .out(in1), .sel(counter_2_q));  // open: en
  Counter #(.width(1), .max('h1), .ongoal("stay")) counter_2 (
    .Q(counter_2_q), .clk(clk), .clr(reset));  // open: load, D, count, carry
  Multiplexer multiplexer_3 (.in0(1'b0), .in1(register_3_q), .out(in0), .sel(counter_3_q));  // open: en
  Counter #(.width(1), .max('h1), .ongoal("stay")) counter_3 (
    .Q(counter_3_q), .clk(clk), .clr(reset));  // open: load, D, count, carry
endmodule

module \状态转移  (
  input  C2,
  input  C1,
  input  C0,
  input  D1,
  input  D0,
  output C22,
  output C12,
  output C02,
  output hit,
  output arrive
);

  wire and_1_out, and_2_out, and_3_out, and_4_out, and_5_out, and_6_out, and_7_out, and_8_out, and_9_out,
       and_10_out, and_11_out, and_12_out, and_13_out, and_14_out, and_15_out, and_16_out, and_17_out,
       and_18_out, and_19_out, and_20_out, not_1_out, not_2_out, not_3_out, not_4_out, not_5_out, not_6_out,
       not_7_out, not_8_out, not_9_out, not_10_out, not_11_out, not_12_out, not_13_out, not_14_out,
       not_15_out, not_16_out, not_17_out, not_18_out, not_19_out, not_20_out, not_21_out, not_22_out,
       not_23_out, not_24_out, not_25_out, not_26_out, not_27_out, not_28_out, not_29_out, not_30_out,
       not_31_out, not_32_out, not_33_out, not_34_out, not_35_out, not_36_out, not_37_out, not_38_out,
       not_39_out, not_40_out, not_41_out, not_42_out, not_43_out, not_44_out, not_45_out, not_46_out,
       not_47_out, not_48_out, not_49_out, not_50_out;

  not not_1 (not_1_out, C2);
  not not_2 (not_2_out, C0);
  not not_3 (not_3_out, D1);
  not not_4 (not_4_out, D0);
  not not_5 (not_5_out, C2);
  not not_6 (not_6_out, D1);
  not not_7 (not_7_out, C2);
  not not_8 (not_8_out, C1);
  not not_9 (not_9_out, D1);
  not not_10 (not_10_out, C2);
  not not_11 (not_11_out, D1);
  not not_12 (not_12_out, D0);
  not not_13 (not_13_out, C2);
  not not_14 (not_14_out, C0);
  not not_15 (not_15_out, D1);
  not not_16 (not_16_out, C2);
  not not_17 (not_17_out, C0);
  not not_18 (not_18_out, D0);
  not not_19 (not_19_out, C2);
  not not_20 (not_20_out, C2);
  not not_21 (not_21_out, C1);
  not not_22 (not_22_out, D1);
  not not_23 (not_23_out, D0);
  not not_24 (not_24_out, C2);
  not not_25 (not_25_out, C2);
  not not_26 (not_26_out, C2);
  not not_27 (not_27_out, D0);
  not not_28 (not_28_out, C2);
  not not_29 (not_29_out, C0);
  not not_30 (not_30_out, D1);
  not not_31 (not_31_out, C2);
  not not_32 (not_32_out, C1);
  not not_33 (not_33_out, C0);
  not not_34 (not_34_out, C2);
  not not_35 (not_35_out, C0);
  not not_36 (not_36_out, D0);
  not not_37 (not_37_out, C2);
  not not_38 (not_38_out, C2);
  not not_39 (not_39_out, D1);
  not not_40 (not_40_out, D0);
  not not_41 (not_41_out, C2);
  not not_42 (not_42_out, C0);
  not not_43 (not_43_out, D1);
  not not_44 (not_44_out, D0);
  not not_45 (not_45_out, C2);
  not not_46 (not_46_out, C0);
  not not_47 (not_47_out, C2);
  not not_48 (not_48_out, D1);
  not not_49 (not_49_out, C2);
  not not_50 (not_50_out, D0);
  and and_1 (and_1_out, not_1_out, C1, not_2_out, not_3_out, not_4_out);
  and and_2 (and_2_out, not_5_out, C1, C0, not_6_out, D0);
  and and_3 (and_3_out, not_7_out, not_8_out, C0, not_9_out);
  and and_4 (and_4_out, not_10_out, C0, not_11_out, not_12_out);
  and and_5 (and_5_out, not_13_out, C1, not_14_out, not_15_out, D0);
  and and_6 (and_6_out, not_16_out, C1, not_17_out, D1, not_18_out);
  and and_7 (and_7_out, not_19_out, C1, C0, D1, D0);
  and and_8 (and_8_out, not_20_out, not_21_out, not_22_out, not_23_out);
  and and_9 (and_9_out, not_24_out, C0, D1, D0);
  and and_10 (and_10_out, not_25_out, C1, D1, D0);
  and and_11 (and_11_out, not_26_out, C1, C0, not_27_out);
  and and_12 (and_12_out, not_28_out, not_29_out, not_30_out, D0);
  and and_13 (and_13_out, not_31_out, not_32_out, not_33_out, D1);
  and and_14 (and_14_out, not_34_out, not_35_out, D1, not_36_out);
  and and_15 (and_15_out, not_37_out, C0, D1, D0);
  and and_16 (and_16_out, not_38_out, C1, C0, not_39_out, not_40_out);
  and and_17 (and_17_out, not_41_out, C1, not_42_out, not_43_out, not_44_out);
  and and_18 (and_18_out, not_45_out, C1, not_46_out, D1, D0);
  and and_19 (and_19_out, not_47_out, C1, C0, not_48_out, D0);
  and and_20 (and_20_out, not_49_out, C1, C0, D1, not_50_out);
  or or_1 (C22, and_1_out, and_2_out);
  or or_2 (C12, and_3_out, and_4_out, and_5_out, and_6_out, and_7_out);
  or or_3 (C02, and_8_out, and_9_out, and_10_out, and_11_out);
  or or_4 (hit, and_12_out, and_13_out, and_14_out, and_15_out, and_16_out);
  or or_5 (arrive, and_17_out, and_18_out, and_19_out, and_20_out);
endmodule
