// Logisim project new_fib.circ as structural Verilog: 1 circuit, main circuit main
module main (
  input  [4:0] in_1,
  output [31:0] out_2
);

  wire clk, counter_1_q, \end , load, not_2_out;
  wire [4:0] adder_1_out, counter_2_q;
  wire [31:0] adder_2_out, and_1_out, shift_register_1_q0, shift_register_1_q1, shift_register_1_q2;

  Counter #(.width(1), .max('h1), .ongoal("stay")) counter_1 (
    .Q(counter_1_q), .clk(clk));  // open: load, D, count, carry, clr
  Clock clock_1 (.out(clk));
  not not_1 (load, counter_1_q);
  Counter #(.width(5), .max('h1f), .ongoal("stay")) counter_2 (
    .Q(counter_2_q), .clk(clk));  // open: load, D, count, carry, clr
  Adder #(.width(5)) adder_1 (.a(counter_2_q), .b(5'b00011), .out(adder_1_out));  // open: cin, cout
  not not_2 (not_2_out, \end );
  // Probe on shift_register_1_q0
  // Probe on shift_register_1_q1
  // Probe on shift_register_1_q2
  // Probe on adder_1_out
  Shift_Register #(.width(32), .length(3)) shift_register_1 (
    .shift(not_2_out), .in(adder_2_out), .clk(clk), .load(load), .d0(32'h1), .q0(shift_register_1_q0),
    .d1(32'h1), .q1(shift_register_1_q1), .d2({32{1'b0}}), .q2(shift_register_1_q2));  // open: out, clr
  Comparator #(.width(5)) comparator_1 (.a(in_1), .b(adder_1_out), .lt(\end ));  // open: gt, eq
  assign and_1_out = shift_register_1_q2 & shift_register_1_q1;  // AND_Gate and_1, 32 bits wide
  Adder #(.width(32)) adder_2 (.a(and_1_out), .b(shift_register_1_q0), .out(adder_2_out));  // open: cin, cout
  // Probe on adder_2_out
  Multiplexer #(.width(32)) multiplexer_1 (.in0({32{1'b0}}), .in1(adder_2_out), .out(out_2), .sel(\end ));  // open: en
endmodule
