// Logisim project 辗转相除法 -1.circ as structural Verilog: 1 circuit, main circuit main
module main (
  input  [31:0] in_1,
  input  [31:0] in_2,
  output [31:0] out_3
);

  wire and_1_out, clock_1_out, comparator_1_lt, comparator_2_eq, counter_1_q, not_1_out;
  wire [31:0] divider_1_rem, multiplexer_1_out, multiplexer_2_out, multiplexer_3_out, multiplexer_4_out,
       register_1_q, register_2_q;

  // Probe on in_1
  // Probe on in_2
  Multiplexer #(.width(32)) multiplexer_1 (
    .in0(in_1), .in1(in_2), .out(multiplexer_1_out), .sel(comparator_1_lt));  // open: en
  Multiplexer #(.width(32)) multiplexer_2 (
    .in0(in_2), .in1(in_1), .out(multiplexer_2_out), .sel(comparator_1_lt));  // open: en
  Comparator #(.width(32), .mode("unsigned")) comparator_1 (.a(in_1), .b(in_2), .lt(comparator_1_lt));  // open: gt, eq
  Clock clock_1 (.out(clock_1_out));
  // Probe on multiplexer_4_out
  Register #(.width(32)) register_1 (.D(multiplexer_4_out), .Q(register_1_q), .clk(clock_1_out));  // open: en, clr
  Register #(.width(32)) register_2 (.D(divider_1_rem), .Q(register_2_q), .clk(clock_1_out));  // open: en, clr
  Counter #(.width(1), .max('h1), .ongoal("stay")) counter_1 (
    .Q(counter_1_q), .clk(clock_1_out));  // open: load, D, count, carry, clr
  Multiplexer #(.width(32)) multiplexer_3 (
    .in0(multiplexer_1_out), .in1(register_1_q), .out(multiplexer_3_out), .sel(counter_1_q));  // open: en
  Multiplexer #(.width(32)) multiplexer_4 (
    .in0(multiplexer_2_out), .in1(register_2_q), .out(multiplexer_4_out), .sel(counter_1_q));  // open: en
  // Probe on multiplexer_3_out
  Divider #(.width(32)) divider_1 (
    .a(multiplexer_3_out), .b(multiplexer_4_out), .rem(divider_1_rem));  // open: out, upper
  // Probe on divider_1_rem
  Comparator #(.width(32), .mode("unsigned")) comparator_2 (
    .a(divider_1_rem), .b({32{1'b0}}), .eq(comparator_2_eq));  // open: gt, lt
  // Probe on multiplexer_4_out
  // Probe on out_3
  Register #(.width(32)) register_3 (.D(multiplexer_4_out), .Q(out_3), .clk(and_1_out));  // open: en, clr
  and and_1 (and_1_out, comparator_2_eq, not_1_out);
  not not_1 (not_1_out, comparator_2_eq);

  // Other names for the same wires on the sheet: A[31:0] = in_1; B[31:0] = in_2
endmodule
