// Logisim project fsm.circ as structural Verilog: 5 circuits, main circuit fsm
module fsm (
  input  in_1,
  input  [1:0] in,
  output out_3
);

  wire clk, \状态存储_1_out_4 , \状态存储_1_out_5 ;
  wire [1:0] multiplexer_1_out, \状态转移_1_c02 ;

  Clock clock_1 (.out(clk));
  \状态转移  \u_状态转移_1  (
    .C1(\状态存储_1_out_4 ), .C0(\状态存储_1_out_5 ), .i1(in[1]), .i0(in[0]), .C12(\状态转移_1_c02 [1]),
    .C02(\状态转移_1_c02 [0]));
  Multiplexer #(.width(2)) multiplexer_1 (
    .in0(\状态转移_1_c02 ), .in1(2'b00), .out(multiplexer_1_out), .sel(in_1));  // open: en
  \状态存储  \u_状态存储_1  (
    .in_1(multiplexer_1_out[1]), .in_2(multiplexer_1_out[0]), .in_3(clk), .out_4(\状态存储_1_out_4 ),
    .out_5(\状态存储_1_out_5 ));
  \状态输出  \u_状态输出_1  (.a(\状态存储_1_out_4 ), .b(\状态存储_1_out_5 ), .c(in[1]), .d(in[0]), .x(out_3));

  // Other names for the same wires on the sheet: clr = in_1
endmodule

module \状态转移  (
  input  C1,
  input  C0,
  input  i1,
  input  i0,
  output C12,
  output C02
);

  wire and_1_out, and_2_out, and_3_out, and_4_out, not_1_out, not_2_out, not_3_out, not_4_out, not_5_out,
       not_6_out, not_7_out;

  not not_1 (not_1_out, C1);
  and and_1 (and_1_out, not_1_out, C0, not_2_out);
  not not_2 (not_2_out, i0);
  and and_2 (and_2_out, C1, not_3_out, not_4_out);
  not not_3 (not_3_out, C0);
  not not_4 (not_4_out, i0);
  not not_5 (not_5_out, i1);
  and and_3 (and_3_out, not_5_out, i0);
  and and_4 (and_4_out, C1, not_6_out, not_7_out);
  not not_6 (not_6_out, C0);
  not not_7 (not_7_out, i0);
  or or_1 (C12, and_1_out, and_2_out);
  or or_2 (C02, and_3_out, and_4_out);
endmodule

module \状态存储  (
  input  in_1,
  input  in_2,
  input  in_3,
  output out_4,
  output out_5
);

  wire counter_1_q, counter_2_q, multiplexer_1_out, multiplexer_2_out;

  Counter #(.width(1), .max('h1), .ongoal("stay")) counter_1 (
    .Q(counter_1_q), .clk(in_3));  // open: load, D, count, carry, clr
  Counter #(.width(1), .max('h1), .ongoal("stay")) counter_2 (
    .Q(counter_2_q), .clk(in_3));  // open: load, D, count, carry, clr
  Register #(.width(1)) register_1 (.D(multiplexer_1_out), .Q(out_4), .clk(in_3));  // open: en, clr
  Multiplexer multiplexer_1 (.in0(1'b0), .in1(in_1), .out(multiplexer_1_out), .sel(counter_1_q));  // open: en
  Multiplexer multiplexer_2 (.in0(1'b0), .in1(in_2), .out(multiplexer_2_out), .sel(counter_2_q));  // open: en
  Register #(.width(1)) register_2 (.D(multiplexer_2_out), .Q(out_5), .clk(in_3));  // open: en, clr

  // Other names for the same wires on the sheet: clk = in_3
endmodule

module Draft (
  input  [1:0] in,
  input  [1:0] in_2
);

  wire clk, clr, \状态存储_1_out_4 , \状态存储_1_out_5 , \状态转移_1_c02 , \状态转移_1_c12 ;
  wire [1:0] multiplexer_1_out;

  Multiplexer #(.width(2)) multiplexer_1 (.in0(in), .in1(2'b00), .out(multiplexer_1_out), .sel(clr));  // open: en
  \状态转移  \u_状态转移_1  (
    .C1(\状态存储_1_out_4 ), .C0(\状态存储_1_out_5 ), .i1(in_2[1]), .i0(in_2[0]), .C12(\状态转移_1_c12 ),
    .C02(\状态转移_1_c02 ));
  \状态存储  \u_状态存储_1  (.in_1(\状态转移_1_c02 ), .in_2(clr), .in_3(clk), .out_4(\状态存储_1_out_4 ), .out_5(\状态存储_1_out_5 ));
endmodule

module \状态输出  (
  input  a,
  input  b,
  input  c,
  input  d,
  output x
);

  wire not_1_out, not_2_out;

  and and_1 (x, a, not_1_out, not_2_out);
  not not_1 (not_1_out, b);
  not not_2 (not_2_out, d);
endmodule
