// Logisim project ftoi_ori.circ as structural Verilog: 1 circuit, main circuit ftoi
module ftoi (
  input  [15:0] in_1,
  output [31:0] out_2
);

  wire comparator_4_lt, lessThanTen, lessThanZero;
  wire [1:0] sel;
  wire [4:0] subtractor_1_out;
  wire [10:10] res;
  wire [31:0] adder_1_out, bit_extender_1_out, bit_extender_2_out, left, multiplexer_2_out, not_2_out, out,
       right;

  Comparator #(.width(5), .mode("unsigned")) comparator_1 (
    .a(in_1[14:10]), .b({5{1'b0}}), .eq(sel[0]));  // open: gt, lt
  Comparator #(.width(5), .mode("unsigned")) comparator_2 (
    .a(in_1[14:10]), .b({5{1'b1}}), .eq(sel[1]));  // open: gt, lt
  Multiplexer #(.select(2), .width(32), .disabled(0)) multiplexer_1 (
    .in0(left), .in1({32{1'b0}}), .in2(right), .out(out), .sel({lessThanTen, lessThanZero}));  // open: in3, en
  Comparator #(.width(5), .mode("unsigned")) comparator_3 (
    .a(in_1[14:10]), .b({5{1'b0}}), .lt(lessThanZero));  // open: gt, eq
  Comparator #(.width(5), .mode("unsigned")) comparator_4 (
    .a(in_1[14:10]), .b(5'b01010), .lt(comparator_4_lt));  // open: gt, eq
  not not_1 (res[10], sel[0]);
  and and_1 (lessThanTen, lessThanZero, comparator_4_lt);
  assign not_2_out = ~out;  // NOT_Gate not_2, 32 bits wide
  Adder #(.width(32)) adder_1 (.a(not_2_out), .b(32'h1), .out(adder_1_out));  // open: cin, cout
  assign bit_extender_1_out = {{21{1'b0}}, {res[10], in_1[9:0]}};  // Bit_Extender bit_extender_1
  Subtractor #(.width(5)) subtractor_1 (.a(in_1[14:10]), .b(5'b01010), .out(subtractor_1_out));  // open: bin, bout
  assign bit_extender_2_out = {{21{1'b0}}, {res[10], in_1[9:0]}};  // Bit_Extender bit_extender_2
  Multiplexer #(.width(32)) multiplexer_2 (
    .in0(out), .in1(adder_1_out), .out(multiplexer_2_out), .sel(in_1[15]));  // open: en
  Shifter #(.width(32)) shifter_1 (.in(bit_extender_1_out), .\dist (subtractor_1_out), .out(left));
  Shifter #(.width(32), .shift("lr")) shifter_2 (.in(bit_extender_2_out), .\dist (in_1[14:10]), .out(right));
  Multiplexer #(.select(2), .width(32), .disabled(0)) multiplexer_3 (
    .in0(multiplexer_2_out), .in1(multiplexer_2_out), .in2({32{1'b0}}), .out(out_2), .sel(sel));  // open: in3, en

  // Other names for the same wires on the sheet: exp[4:0] = in_1[14:10]; s = in_1[15]; fraction[9:0] = in_1[9:0];
  //   res[9:0] = in_1[9:0]
endmodule
