// Logisim project string.circ as structural Verilog: 6 circuits, main circuit string
module \string  (
  input  [1:0] in_1,
  input  in_2,
  output [1:0] out_3
);

  wire in1, in2, in3, in4, in5, in6, \状态转移1_1_x , \状态转移1_1_y , \状态转移1_1_z , \状态转移2_1_x , \状态转移2_1_y ,
       \状态转移2_1_z ;
  wire [1:0] out, out1, out2;

  \状态转移1  \u_状态转移1_1  (
    .a(in1), .b(in2), .c(in3), .d(in_1[1]), .e(in_1[0]), .x(\状态转移1_1_x ), .y(\状态转移1_1_y ), .z(\状态转移1_1_z ));
  \状态转移2  \u_状态转移2_1  (
    .a(in4), .b(in5), .c(in6), .d(in_1[1]), .e(in_1[0]), .x(\状态转移2_1_x ), .y(\状态转移2_1_y ), .z(\状态转移2_1_z ));
  \状态存储  \u_状态存储_1  (.in_1(\状态转移1_1_x ), .in_2(in_2), .out_3(in1));
  \状态存储  \u_状态存储_2  (.in_1(\状态转移1_1_y ), .in_2(in_2), .out_3(in2));
  \状态存储  \u_状态存储_3  (.in_1(\状态转移1_1_z ), .in_2(in_2), .out_3(in3));
  \状态输出1  \u_状态输出1_1  (.a(in1), .b(in2), .c(in3), .d(in_1[1]), .e(in_1[0]), .x(out1[1]), .y(out1[0]));
  \状态存储  \u_状态存储_4  (.in_1(\状态转移2_1_x ), .in_2(in_2), .out_3(in4));
  \状态存储  \u_状态存储_5  (.in_1(\状态转移2_1_y ), .in_2(in_2), .out_3(in5));
  \状态存储  \u_状态存储_6  (.in_1(\状态转移2_1_z ), .in_2(in_2), .out_3(in6));
  \状态输出2  \u_状态输出2_1  (.a(in4), .b(in5), .c(in6), .d(in_1[1]), .e(in_1[0]), .x(out2[1]), .y(out2[0]));
  // Probe on out1
  // Probe on out2
  Comparator #(.width(2), .mode("unsigned")) comparator_1 (.a(out1), .b(2'b01), .eq(out[0]));  // open: gt, lt
  Comparator #(.width(2), .mode("unsigned")) comparator_2 (.a(out2), .b(2'b10), .eq(out[1]));  // open: gt, lt
  Multiplexer #(.select(2), .width(2)) multiplexer_1 (
    .in0(2'b00), .in1(2'b01), .in2(2'b10), .in3(2'b00), .out(out_3), .sel(out));  // open: en

  // Other names for the same wires on the sheet: reset = in_2
endmodule

module \状态转移1  (
  input  a,
  input  b,
  input  c,
  input  d,
  input  e,
  output x,
  output y,
  output z
);

  wire and_2_out, and_3_out, not_1_out, not_2_out, not_3_out;

  not not_1 (not_1_out, d);
  not not_2 (not_2_out, e);
  not not_3 (not_3_out, c);
  and and_1 (x, b, c, not_1_out, not_2_out);
  and and_2 (and_2_out, c, d);
  and and_3 (and_3_out, b, not_3_out, e);
  or or_1 (y, and_2_out, and_3_out);

  assign z = e;
endmodule

module \状态输出1  (
  input  a,
  input  b,
  input  c,
  input  d,
  input  e,
  output x,
  output y
);

  wire and_1_out, and_2_out, and_3_out, and_4_out, and_5_out, and_6_out, not_1_out, not_2_out, not_3_out,
       not_4_out, not_5_out, not_6_out, not_7_out, not_8_out;

  not not_1 (not_1_out, a);
  not not_2 (not_2_out, b);
  not not_3 (not_3_out, c);
  not not_4 (not_4_out, a);
  not not_5 (not_5_out, b);
  not not_6 (not_6_out, c);
  not not_7 (not_7_out, d);
  not not_8 (not_8_out, e);
  and and_1 (and_1_out, not_1_out, not_2_out, d, e);
  and and_2 (and_2_out, b, not_3_out, d, e);
  and and_3 (and_3_out, a, c, d, e);
  and and_4 (and_4_out, not_4_out, b, c, d, e);
  and and_5 (and_5_out, a, not_5_out, not_6_out);
  and and_6 (and_6_out, a, b, c, not_7_out, not_8_out);
  or or_1 (x, and_1_out, and_2_out, and_3_out);
  or or_2 (y, and_4_out, and_5_out, and_6_out);
endmodule

module \状态转移2  (
  input  a,
  input  b,
  input  c,
  input  d,
  input  e,
  output x,
  output y,
  output z
);

  wire and_1_out, and_2_out, and_3_out, and_4_out, and_5_out, and_6_out, not_1_out, not_2_out, not_3_out,
       not_4_out, not_5_out, not_6_out, not_7_out;

  not not_1 (not_1_out, a);
  not not_2 (not_2_out, b);
  not not_3 (not_3_out, c);
  not not_4 (not_4_out, d);
  not not_5 (not_5_out, e);
  not not_6 (not_6_out, c);
  not not_7 (not_7_out, e);
  and and_1 (and_1_out, not_1_out, b, c, e);
  and and_2 (and_2_out, a, b, c, d);
  and and_3 (and_3_out, not_2_out, c, e);
  and and_4 (and_4_out, b, not_3_out, d);
  and and_5 (and_5_out, not_4_out, not_5_out);
  and and_6 (and_6_out, b, not_6_out, not_7_out);
  or or_1 (x, and_1_out, and_2_out);
  or or_2 (y, and_3_out, and_4_out);
  or or_3 (z, and_5_out, and_6_out);
endmodule

module \状态输出2  (
  input  a,
  input  b,
  input  c,
  input  d,
  input  e,
  output x,
  output y
);

  wire and_1_out, and_2_out, and_3_out, not_1_out, not_2_out, not_3_out, not_4_out, not_5_out, not_6_out;

  not not_1 (not_1_out, b);
  not not_2 (not_2_out, c);
  not not_3 (not_3_out, d);
  not not_4 (not_4_out, b);
  not not_5 (not_5_out, c);
  not not_6 (not_6_out, e);
  and and_1 (and_1_out, a, not_1_out, not_2_out, not_3_out);
  and and_2 (and_2_out, a, not_4_out, not_5_out, not_6_out);
  and and_3 (and_3_out, a, b, c, d);
  or or_1 (x, and_1_out, and_2_out, and_3_out);

  assign y = 1'b0;
endmodule

module \状态存储  (
  input  in_1,
  input  in_2,
  output out_3
);

  wire clock_1_out, clock_2_out, counter_1_q, register_1_q;

  Register #(.width(1)) register_1 (.D(in_1), .Q(register_1_q), .clk(clock_1_out), .clr(in_2));  // open: en
  Clock clock_1 (.out(clock_1_out));
  Clock clock_2 (.out(clock_2_out));
  Multiplexer multiplexer_1 (.in0(1'b0), .in1(register_1_q), .out(out_3), .sel(counter_1_q));  // open: en
  Counter #(.width(1), .max('h1), .ongoal("stay")) counter_1 (
    .Q(counter_1_q), .clk(clock_2_out), .clr(in_2));  // open: load, D, count, carry

  // Other names for the same wires on the sheet: reset = in_2
endmodule
