// Logisim project tmp.circ as structural Verilog: 1 circuit, main circuit CRC
module CRC (
  output [1:0] out_1
);

  wire clock_1_out;

  Counter #(.width(2), .max('h3), .ongoal("continue")) counter_1 (
    .Q(out_1), .clk(clock_1_out));  // open: load, D, count, carry, clr
  Clock clock_1 (.out(clock_1_out));
endmodule
