// Logisim project 移位寄存器.circ as structural Verilog: 1 circuit, main circuit 辗转相除法
module \辗转相除法  (
  input  [7:0] in_1,
  input  [7:0] in_2,
  output [7:0] out_3
);

  wire clk, comparator_2_eq, counter_1_q, \end , load, not_2_out;
  wire [7:0] rem, shift_register_1_q0, shift_register_1_q1;

  Clock clock_1 (.out(clk));
  Counter #(.width(1), .max('h1), .ongoal("stay")) counter_1 (
    .Q(counter_1_q), .clk(clk));  // open: load, D, count, carry, clr
  not not_1 (load, counter_1_q);
  not not_2 (not_2_out, \end );
  Shift_Register #(.width(8), .length(2)) shift_register_1 (
    .shift(not_2_out), .in(rem), .clk(clk), .load(load), .d0(in_2), .q0(shift_register_1_q0), .d1(in_1),
    .q1(shift_register_1_q1));  // open: out, clr
  Comparator comparator_1 (.a(rem), .b({8{1'b0}}), .eq(\end ));  // open: gt, lt
  Divider divider_1 (.a(shift_register_1_q1), .b(shift_register_1_q0), .rem(rem));  // open: out, upper
  Multiplexer #(.width(8)) multiplexer_1 (
    .in0({8{1'b0}}), .in1(shift_register_1_q0), .out(out_3), .sel(\end ));  // open: en
  Multiplexer #(.width(4)) multiplexer_2 (.in1(4'b0001), .sel(comparator_2_eq));  // open: in0, out, en
  Comparator comparator_2 (.a(in_1), .b(8'h1), .eq(comparator_2_eq));  // open: gt, lt

  // Other names for the same wires on the sheet: a[7:0] = in_1; b[7:0] = in_2
endmodule
