// Logisim project mealy.circ as structural Verilog: 4 circuits, main circuit main
module main (
  input  [1:0] in_1,
  input  in_2,
  input  in_3,
  output [3:0] out_4
);

  wire statestore_1_out_6, statestore_1_out_7, statestore_1_out_8, statetrans_1_x, statetrans_1_y,
       statetrans_1_z;
  wire [2:0] statetrans_2_z;

  StateTrans statetrans_1 (
    .a(statestore_1_out_6), .b(statestore_1_out_7), .c(statestore_1_out_8), .d(in_1[1]), .e(in_1[0]),
    .x(statetrans_1_x), .y(statetrans_1_y), .z(statetrans_1_z));
  StateStore statestore_1 (
    .in_1(statetrans_1_x), .in_2(statetrans_1_y), .in_3(statetrans_1_z), .in_4(in_3), .in_5(in_2),
    .out_6(statestore_1_out_6), .out_7(statestore_1_out_7), .out_8(statestore_1_out_8));
  StateTrans statetrans_2 (
    .a(statestore_1_out_6), .b(statestore_1_out_7), .c(statestore_1_out_8), .d(in_1[1]), .e(in_1[0]),
    .x(statetrans_2_z[2]), .y(statetrans_2_z[1]), .z(statetrans_2_z[0]));
  // Probe on {1'b0, statetrans_2_z}
  Adder #(.width(4)) adder_1 (.a({1'b0, statetrans_2_z}), .b(4'b0001), .out(out_4));  // open: cin, cout

  // Other names for the same wires on the sheet: clk = in_3; rst = in_2
endmodule

module StateTrans (
  input  a,
  input  b,
  input  c,
  input  d,
  input  e,
  output x,
  output y,
  output z
);

  wire and_1_out, and_2_out, and_3_out, and_4_out, and_5_out, and_6_out, and_7_out, and_8_out, and_9_out,
       and_10_out, and_11_out, and_12_out, and_13_out, and_14_out, and_15_out, and_16_out, and_17_out,
       and_18_out, and_19_out, and_20_out, not_1_out, not_2_out, not_3_out, not_4_out, not_5_out, not_6_out,
       not_7_out, not_8_out, not_9_out, not_10_out, not_11_out, not_12_out, not_13_out, not_14_out,
       not_15_out, not_16_out, not_17_out, not_18_out, not_19_out, not_20_out, not_21_out, not_22_out,
       not_23_out, not_24_out, not_25_out, not_26_out, not_27_out, not_28_out, not_29_out, not_30_out,
       not_31_out, not_32_out, not_33_out, not_34_out, not_35_out, not_36_out;

  not not_1 (not_1_out, b);
  not not_2 (not_2_out, c);
  not not_3 (not_3_out, e);
  not not_4 (not_4_out, e);
  not not_5 (not_5_out, d);
  not not_6 (not_6_out, b);
  not not_7 (not_7_out, c);
  not not_8 (not_8_out, a);
  not not_9 (not_9_out, c);
  not not_10 (not_10_out, e);
  not not_11 (not_11_out, a);
  not not_12 (not_12_out, d);
  not not_13 (not_13_out, a);
  not not_14 (not_14_out, d);
  not not_15 (not_15_out, c);
  not not_16 (not_16_out, d);
  not not_17 (not_17_out, e);
  not not_18 (not_18_out, e);
  not not_19 (not_19_out, a);
  not not_20 (not_20_out, b);
  not not_21 (not_21_out, c);
  not not_22 (not_22_out, d);
  not not_23 (not_23_out, a);
  not not_24 (not_24_out, b);
  not not_25 (not_25_out, e);
  not not_26 (not_26_out, b);
  not not_27 (not_27_out, a);
  not not_28 (not_28_out, c);
  not not_29 (not_29_out, e);
  not not_30 (not_30_out, d);
  not not_31 (not_31_out, b);
  not not_32 (not_32_out, c);
  not not_33 (not_33_out, d);
  not not_34 (not_34_out, e);
  not not_35 (not_35_out, b);
  not not_36 (not_36_out, c);
  and and_1 (and_1_out, not_1_out, not_2_out, d, not_3_out);
  and and_2 (and_2_out, b, c, d, not_4_out);
  and and_3 (and_3_out, a, not_5_out);
  and and_4 (and_4_out, a, not_6_out, c);
  and and_5 (and_5_out, a, b, not_7_out);
  and and_6 (and_6_out, not_8_out, not_9_out, d, not_10_out);
  and and_7 (and_7_out, not_11_out, c, not_12_out, e);
  and and_8 (and_8_out, not_13_out, b, e);
  and and_9 (and_9_out, b, c, not_14_out);
  and and_10 (and_10_out, a, not_15_out, d, e);
  and and_11 (and_11_out, a, c, not_16_out, not_17_out);
  and and_12 (and_12_out, a, b, not_18_out);
  and and_13 (and_13_out, not_19_out, not_20_out, not_21_out, not_22_out, e);
  and and_14 (and_14_out, not_23_out, not_24_out, d, not_25_out);
  and and_15 (and_15_out, not_26_out, c, d);
  and and_16 (and_16_out, not_27_out, b, not_28_out, not_29_out);
  and and_17 (and_17_out, b, c, not_30_out);
  and and_18 (and_18_out, a, not_31_out, not_32_out, not_33_out, not_34_out);
  and and_19 (and_19_out, a, not_35_out, d, e);
  and and_20 (and_20_out, a, b, not_36_out, e);
  or or_1 (x, and_1_out, and_2_out, and_3_out, and_4_out, and_5_out);
  or or_2 (y, and_6_out, and_7_out, and_8_out, and_9_out, and_10_out, and_11_out, and_12_out);
  or or_3 (z, and_13_out, and_14_out, and_15_out, and_16_out, and_17_out, and_18_out, and_19_out, and_20_out);
endmodule

module StateStore (
  input  in_1,
  input  in_2,
  input  in_3,
  input  in_4,
  input  in_5,
  output out_6,
  output out_7,
  output out_8
);

  Register #(.width(1)) register_1 (.D(in_1), .Q(out_6), .clk(in_4), .clr(in_5));  // open: en
  Register #(.width(1)) register_2 (.D(in_2), .Q(out_7), .clk(in_4), .clr(in_5));  // open: en
  Register #(.width(1)) register_3 (.D(in_3), .Q(out_8), .clk(in_4), .clr(in_5));  // open: en

  // Other names for the same wires on the sheet: clk = in_4; rst = in_5
endmodule

module test (
  output [3:0] out_1
);

  Adder #(.width(4)) adder_1 (.a(4'b0111), .b(4'b0001), .out(out_1));  // open: cin, cout
endmodule
