// Logisim project nonexist.circ as structural Verilog: 6 circuits, main circuit main
module main (
  input  [7:0] in_1,
  input  [7:0] in_2,
  input  [7:0] in_3,
  input  [7:0] in_4,
  input  [7:0] in_5,
  output [7:0] out_6
);

  wire _1, _2, _3, _4, _5;
  wire [7:0] multiplexer_1_out, multiplexer_2_out, multiplexer_3_out, multiplexer_4_out;

  has1 has1_1 (.in_1(in_1), .in_2(in_2), .in_3(in_3), .in_4(in_4), .in_5(in_5), .out_6(_1));
  has4 has4_1 (.in_1(in_1), .in_2(in_2), .in_3(in_3), .in_4(in_4), .in_5(in_5), .out_6(_4));
  Multiplexer #(.width(8)) multiplexer_1 (.in0(8'h5), .in1(8'h6), .out(multiplexer_1_out), .sel(_5));  // open: en
  has2 has2_1 (.in_1(in_1), .in_2(in_2), .in_3(in_3), .in_4(in_4), .in_5(in_5), .out_6(_2));
  Multiplexer #(.width(8)) multiplexer_2 (
    .in0(8'h4), .in1(multiplexer_1_out), .out(multiplexer_2_out), .sel(_4));  // open: en
  Multiplexer #(.width(8)) multiplexer_3 (
    .in0(8'h3), .in1(multiplexer_2_out), .out(multiplexer_3_out), .sel(_3));  // open: en
  Multiplexer #(.width(8)) multiplexer_4 (
    .in0(8'h2), .in1(multiplexer_3_out), .out(multiplexer_4_out), .sel(_2));  // open: en
  has3 has3_1 (.in_1(in_1), .in_2(in_2), .in_3(in_3), .in_4(in_4), .in_5(in_5), .out_6(_3));
  has5 has5_1 (.in_1(in_1), .in_2(in_2), .in_3(in_3), .in_4(in_4), .in_5(in_5), .out_6(_5));
  Multiplexer #(.width(8)) multiplexer_5 (.in0(8'h1), .in1(multiplexer_4_out), .out(out_6), .sel(_1));  // open: en

  // Other names for the same wires on the sheet: a[7:0] = in_1; b[7:0] = in_2; c[7:0] = in_3; d[7:0] = in_4;
  //   e[7:0] = in_5
endmodule

module has1 (
  input  [7:0] in_1,
  input  [7:0] in_2,
  input  [7:0] in_3,
  input  [7:0] in_4,
  input  [7:0] in_5,
  output out_6
);

  wire comparator_1_eq, comparator_2_eq, comparator_3_eq, comparator_4_eq, comparator_5_eq;

  Comparator comparator_1 (.a(in_1), .b(8'h1), .eq(comparator_1_eq));  // open: gt, lt
  Comparator comparator_2 (.a(in_2), .b(8'h1), .eq(comparator_2_eq));  // open: gt, lt
  Comparator comparator_3 (.a(in_3), .b(8'h1), .eq(comparator_3_eq));  // open: gt, lt
  Comparator comparator_4 (.a(in_4), .b(8'h1), .eq(comparator_4_eq));  // open: gt, lt
  Comparator comparator_5 (.a(in_5), .b(8'h1), .eq(comparator_5_eq));  // open: gt, lt
  or or_1 (out_6, comparator_1_eq, comparator_2_eq, comparator_3_eq, comparator_4_eq, comparator_5_eq);
endmodule

module has2 (
  input  [7:0] in_1,
  input  [7:0] in_2,
  input  [7:0] in_3,
  input  [7:0] in_4,
  input  [7:0] in_5,
  output out_6
);

  wire comparator_1_eq, comparator_2_eq, comparator_3_eq, comparator_4_eq, comparator_5_eq;

  Comparator comparator_1 (.a(in_1), .b(8'h2), .eq(comparator_1_eq));  // open: gt, lt
  Comparator comparator_2 (.a(in_2), .b(8'h2), .eq(comparator_2_eq));  // open: gt, lt
  Comparator comparator_3 (.a(in_3), .b(8'h2), .eq(comparator_3_eq));  // open: gt, lt
  Comparator comparator_4 (.a(in_4), .b(8'h2), .eq(comparator_4_eq));  // open: gt, lt
  Comparator comparator_5 (.a(in_5), .b(8'h2), .eq(comparator_5_eq));  // open: gt, lt
  or or_1 (out_6, comparator_1_eq, comparator_2_eq, comparator_3_eq, comparator_4_eq, comparator_5_eq);
endmodule

module has3 (
  input  [7:0] in_1,
  input  [7:0] in_2,
  input  [7:0] in_3,
  input  [7:0] in_4,
  input  [7:0] in_5,
  output out_6
);

  wire comparator_1_eq, comparator_2_eq, comparator_3_eq, comparator_4_eq, comparator_5_eq;

  Comparator comparator_1 (.a(in_1), .b(8'h3), .eq(comparator_1_eq));  // open: gt, lt
  Comparator comparator_2 (.a(in_2), .b(8'h3), .eq(comparator_2_eq));  // open: gt, lt
  Comparator comparator_3 (.a(in_3), .b(8'h3), .eq(comparator_3_eq));  // open: gt, lt
  Comparator comparator_4 (.a(in_4), .b(8'h3), .eq(comparator_4_eq));  // open: gt, lt
  Comparator comparator_5 (.a(in_5), .b(8'h3), .eq(comparator_5_eq));  // open: gt, lt
  or or_1 (out_6, comparator_1_eq, comparator_2_eq, comparator_3_eq, comparator_4_eq, comparator_5_eq);
endmodule

module has4 (
  input  [7:0] in_1,
  input  [7:0] in_2,
  input  [7:0] in_3,
  input  [7:0] in_4,
  input  [7:0] in_5,
  output out_6
);

  wire comparator_1_eq, comparator_2_eq, comparator_3_eq, comparator_4_eq, comparator_5_eq;

  Comparator comparator_1 (.a(in_1), .b(8'h4), .eq(comparator_1_eq));  // open: gt, lt
  Comparator comparator_2 (.a(in_2), .b(8'h4), .eq(comparator_2_eq));  // open: gt, lt
  Comparator comparator_3 (.a(in_3), .b(8'h4), .eq(comparator_3_eq));  // open: gt, lt
  Comparator comparator_4 (.a(in_4), .b(8'h4), .eq(comparator_4_eq));  // open: gt, lt
  Comparator comparator_5 (.a(in_5), .b(8'h4), .eq(comparator_5_eq));  // open: gt, lt
  or or_1 (out_6, comparator_1_eq, comparator_2_eq, comparator_3_eq, comparator_4_eq, comparator_5_eq);
endmodule

module has5 (
  input  [7:0] in_1,
  input  [7:0] in_2,
  input  [7:0] in_3,
  input  [7:0] in_4,
  input  [7:0] in_5,
  output out_6
);

  wire comparator_1_eq, comparator_2_eq, comparator_3_eq, comparator_4_eq, comparator_5_eq;

  Comparator comparator_1 (.a(in_1), .b(8'h5), .eq(comparator_1_eq));  // open: gt, lt
  Comparator comparator_2 (.a(in_2), .b(8'h5), .eq(comparator_2_eq));  // open: gt, lt
  Comparator comparator_3 (.a(in_3), .b(8'h5), .eq(comparator_3_eq));  // open: gt, lt
  Comparator comparator_4 (.a(in_4), .b(8'h5), .eq(comparator_4_eq));  // open: gt, lt
  Comparator comparator_5 (.a(in_5), .b(8'h5), .eq(comparator_5_eq));  // open: gt, lt
  or or_1 (out_6, comparator_1_eq, comparator_2_eq, comparator_3_eq, comparator_4_eq, comparator_5_eq);
endmodule
