// Logisim project main.circ as structural Verilog: 10 circuits, main circuit main
module main (
  input  in_1,
  output [31:0] out_2,
  output [31:0] out_3,
  output out_4,
  output [4:0] out_5,
  output [31:0] out_6,
  output out_7,
  output [31:0] out_8,
  output [31:0] out_9
);

  wire ALUSrc, beq, bgtz, clk, Greater, Less, MemRead, Zero;
  wire [1:0] EXTControl, RegDst;
  wire [2:0] ALUControl, Mem2Reg, NPCControl;
  wire [4:0] rd, rs, rt, shamt;
  wire [5:0] splitter_1_funct, splitter_1_opcode;
  wire [7:0] multiplexer_4_out;
  wire [15:0] Imm16, multiplexer_5_out;
  wire [25:0] Imm26;
  wire [31:0] ByteData, EXTImm32, GRF_rs, HalfData, MemReadData, multiplexer_3_out, NPC, PC, PC_4;

  Clock clock_1 (.out(clk));
  NPC npc_1 (
    .in_5(PC), .in_6(Imm26), .EXTImm32(EXTImm32), .reset(in_1), .NPCControl(NPCControl), .Zero(Zero),
    .out_11(NPC), .GRF_rs(GRF_rs), .out_12(PC_4), ._0(Greater), .in_3(beq), .in_4(bgtz));
  Adder #(.width(32)) adder_1 (.a(PC), .b(32'h3000), .out(out_3));  // open: cin, cout
  IFU ifu_1 (.out_4(out_2), .clk(clk), .reset(in_1), .NPC(NPC), .PC(PC));
  Splitter splitter_1 (
    .Instr(out_2), .opcode(splitter_1_opcode), .rs(rs), .rt(rt), .rd(rd), .shamt(shamt),
    .funct(splitter_1_funct), .Imm26(Imm26), .Imm16(Imm16));
  // Probe on out_8
  // Probe on Imm16
  // Probe on Imm26
  // Probe on EXTImm32
  // Probe on rs
  // Probe on rt
  // Probe on rd
  // Probe on NPC
  // Probe on PC
  Multiplexer #(.select(2), .width(5)) multiplexer_1 (
    .in0(rt), .in1(rd), .in2({5{1'b1}}), .out(out_5), .sel(RegDst));  // open: in3, en
  Multiplexer #(.select(3), .width(32)) multiplexer_2 (
    .in0(out_8), .in1(MemReadData), .in2(EXTImm32), .in3(PC_4), .in4(ByteData), .in5(HalfData), .out(out_6),
    .sel(Mem2Reg));  // open: in6, in7, en
  Controller controller_1 (
    .opcode(splitter_1_opcode), .funct(splitter_1_funct), .ALUControl(ALUControl), .MemRead(MemRead),
    .MemWrite(out_7), .NPCControl(NPCControl), .Mem2Reg(Mem2Reg), .EXTControl(EXTControl), .RegDst(RegDst),
    .ALUSrc(ALUSrc), .RegWrite(out_4), .out_3(beq), .out_4(bgtz));
  GRF grf_1 (
    .in_4(rs), .in_5(rt), .in_6(out_5), .in_7(out_6), .out_8(GRF_rs), .out_9(out_9), .in_1(clk), .in_2(in_1),
    .in_3(out_4));
  // Probe on EXTImm32
  // Probe on ALUControl
  // Probe on NPCControl
  Multiplexer #(.width(32)) multiplexer_3 (
    .in0(out_9), .in1(EXTImm32), .out(multiplexer_3_out), .sel(ALUSrc));  // open: en
  EXT ext_1 (.in_2(Imm16), .out_3(EXTImm32), .EXTControl(EXTControl));
  // Probe on MemReadData
  // Probe on Mem2Reg
  // Probe on EXTControl
  // Probe on out_8
  ALU alu_1 (
    .in_2(GRF_rs), .in_3(multiplexer_3_out), .ALUOut(out_8), .Zero(Zero), .in_1(ALUControl), .in_4(shamt),
    .GreaterZero(Greater), .LessZero(Less));
  // Probe on shamt
  Multiplexer #(.select(2), .width(8)) multiplexer_4 (
    .in0(MemReadData[7:0]), .in1(MemReadData[15:8]), .in2(MemReadData[23:16]), .in3(MemReadData[31:24]),
    .out(multiplexer_4_out), .sel(out_8[1:0]));  // open: en
  Multiplexer #(.width(16)) multiplexer_5 (
    .in0(MemReadData[15:0]), .in1(MemReadData[31:16]), .out(multiplexer_5_out), .sel(out_8[1]));  // open: en
  assign ByteData = {{24{multiplexer_4_out[7]}}, multiplexer_4_out};  // Bit_Extender bit_extender_1
  assign HalfData = {{16{multiplexer_5_out[15]}}, multiplexer_5_out};  // Bit_Extender bit_extender_2
  DM dm_1 (.WD(out_9), .out_7(MemReadData), .in_1(clk), .in_2(in_1), .in_3(out_7), .in_4(MemRead), .A(out_8));

  // Other names for the same wires on the sheet: byte[1:0] = out_8[1:0]; MemAddr[31:0] = out_8; Result[31:0] = out_8;
  //   half = out_8[1]; Instr[31:0] = out_2; MemData[31:0] = out_9; MemWrite = out_7; RegAddr[4:0] = out_5;
  //   RegData[31:0] = out_6; RegWrite = out_4; reset = in_1

  // Notes on the sheet:
  //   新增支持j/jal/jalr/jr/sll指令
endmodule

module NPC (
  input  reset,
  input  [2:0] NPCControl,
  input  in_3,
  input  in_4,
  input  [31:0] in_5,
  input  [25:0] in_6,
  input  [31:0] EXTImm32,
  input  [31:0] GRF_rs,
  input  Zero,
  input  _0,
  output [31:0] out_11,
  output [31:0] out_12
);

  wire Compare;
  wire [0:0] and_1_out;
  wire [15:0] IMM16;
  wire [27:0] bit_extender_1_out, shifter_1_out;
  wire [31:0] adder_2_out, shifter_2_out;

  assign bit_extender_1_out = {{2{1'b0}}, in_6};  // Bit_Extender bit_extender_1
  Shifter #(.width(28)) shifter_1 (.in(bit_extender_1_out), .\dist (5'b00010), .out(shifter_1_out));
  Adder #(.width(32)) adder_1 (.a(in_5), .b(32'h4), .out(out_12));  // open: cin, cout
  Shifter #(.width(32)) shifter_2 (.in(EXTImm32), .\dist (5'b00010), .out(shifter_2_out));
  Bit_Extender #(.in_width(26)) bit_extender_2 (.in(in_6), .out(IMM16));
  Adder #(.width(32)) adder_2 (.a(out_12), .b(shifter_2_out), .out(adder_2_out));  // open: cin, cout
  Multiplexer #(.select(2)) multiplexer_1 (
    .in0(1'b1), .in1(Zero), .in2(_0), .out(Compare), .sel({in_4, in_3}));  // open: in3, en
  Multiplexer #(.select(3), .width(32)) multiplexer_2 (
    .in0(out_12), .in1(adder_2_out), .in2({in_5[31:28], shifter_1_out}), .in4(GRF_rs), .out(out_11),
    .sel({NPCControl[2:1], and_1_out[0]}));  // open: in3, in5, in6, in7, en
  // Probe on {NPCControl[2:1], and_1_out[0]}
  // Probe on NPCControl
  and and_1 (and_1_out[0], NPCControl[0], Compare);

  // Other names for the same wires on the sheet: beq = in_3; bgtz = in_4; PC[31:0] = in_5; IMM26[25:0] = in_6;
  //   PC_4[31:0] = out_12
endmodule

module IFU (
  input  clk,
  input  reset,
  input  [31:0] NPC,
  output [31:0] out_4,
  output [31:0] PC
);

  wire [11:0] bit_extender_1_out;
  wire [31:0] shifter_1_out;

  Register #(.width(32)) register_1 (.D(NPC), .Q(PC), .clk(clk), .clr(reset));  // open: en
  Shifter #(.width(32), .shift("lr")) shifter_1 (.in(PC), .\dist (5'b00010), .out(shifter_1_out));
  Bit_Extender #(.in_width(32), .out_width(12)) bit_extender_1 (.in(shifter_1_out), .out(bit_extender_1_out));
  ROM #(.addrWidth(12), .dataWidth(32)) rom_1 (.addr(bit_extender_1_out), .data(out_4));  // open: sel
  ROM #(.addrWidth(5), .dataWidth(32)) rom_2 ();  // open: addr, data, sel

  // Notes on the sheet:
  //   contents of rom_1 (hex, n*v repeats v):
  //   341c0000 341d0000 34013456 210820 8c010004 ac010004 3c027878 411822 3c051234 34040005 0 ac85ffff
  //   8c83ffff 10650001 1000000d 34670404 10e3000b 0 3c087777 3508ffff 80022 34001100 e65020 34080000
  //   34090001 340a0001 10a4020 1109fffe 1000ffff
  //   contents of rom_2 (hex, n*v repeats v):
  //   340407cf 3485006f 3c063039 3c07ffff 34e7ffff 858021 e78821 f09021 928023 e78823 e49023 2519823
  //   34080000 ad040000 0 ad050004 ad100008 ad11000c ad120010 8d0f0000 8d0e0014 ad0e0018 8d0d000c 35080001
  //   35290001 354a0002 110affef 11090001 3c0b0457 10f4021
endmodule

module GRF (
  input  in_1,
  input  in_2,
  input  in_3,
  input  [4:0] in_4,
  input  [4:0] in_5,
  input  [4:0] in_6,
  input  [31:0] in_7,
  output [31:0] out_8,
  output [31:0] out_9
);

  wire [31:0] i0, i1, i2, i3, i4, i5, i6, i7, i8, i9, i10, i11, i12, i13, i14, i15, i16, i17, i18, i19, i20,
       i21, i22, i23, i24, i25, i26, i27, i28, i29, i30, i31, o1, o2, o3, o4, o5, o6, o7, o8, o9, o10, o11,
       o12, o13, o14, o15, o16, o17, o18, o19, o20, o21, o22, o23, o24, o25, o26, o27, o28, o29, o30, o31,
       register_1_q;

  Register #(.width(32)) register_1 (.D(i0), .en(in_3), .Q(register_1_q), .clk(in_1), .clr(in_2));
  Register #(.width(32)) register_2 (.D(i4), .en(in_3), .Q(o4), .clk(in_1), .clr(in_2));
  Register #(.width(32)) register_3 (.D(i8), .en(in_3), .Q(o8), .clk(in_1), .clr(in_2));
  Register #(.width(32)) register_4 (.D(i12), .en(in_3), .Q(o12), .clk(in_1), .clr(in_2));
  Register #(.width(32)) register_5 (.D(i16), .en(in_3), .Q(o16), .clk(in_1), .clr(in_2));
  Register #(.width(32)) register_6 (.D(i20), .en(in_3), .Q(o20), .clk(in_1), .clr(in_2));
  Register #(.width(32)) register_7 (.D(i24), .en(in_3), .Q(o24), .clk(in_1), .clr(in_2));
  Register #(.width(32)) register_8 (.D(i28), .en(in_3), .Q(o28), .clk(in_1), .clr(in_2));
  Demultiplexer #(.select(5), .width(32), .tristate("true")) demultiplexer_1 (
    .out0(i0), .out1(i1), .out2(i2), .out3(i3), .out4(i4), .out5(i5), .out6(i6), .out7(i7), .out8(i8),
    .out9(i9), .out10(i10), .out11(i11), .out12(i12), .out13(i13), .out14(i14), .out15(i15), .out16(i16),
    .out17(i17), .out18(i18), .out19(i19), .out20(i20), .out21(i21), .out22(i22), .out23(i23), .out24(i24),
    .out25(i25), .out26(i26), .out27(i27), .out28(i28), .out29(i29), .out30(i30), .out31(i31), .in(in_7),
    .sel(in_6));  // open: en
  Register #(.width(32)) register_9 (.D(i1), .en(in_3), .Q(o1), .clk(in_1), .clr(in_2));
  Register #(.width(32)) register_10 (.D(i5), .en(in_3), .Q(o5), .clk(in_1), .clr(in_2));
  Register #(.width(32)) register_11 (.D(i9), .en(in_3), .Q(o9), .clk(in_1), .clr(in_2));
  Register #(.width(32)) register_12 (.D(i13), .en(in_3), .Q(o13), .clk(in_1), .clr(in_2));
  Register #(.width(32)) register_13 (.D(i17), .en(in_3), .Q(o17), .clk(in_1), .clr(in_2));
  Register #(.width(32)) register_14 (.D(i21), .en(in_3), .Q(o21), .clk(in_1), .clr(in_2));
  Register #(.width(32)) register_15 (.D(i25), .en(in_3), .Q(o25), .clk(in_1), .clr(in_2));
  Register #(.width(32)) register_16 (.D(i29), .en(in_3), .Q(o29), .clk(in_1), .clr(in_2));
  Register #(.width(32)) register_17 (.D(i2), .en(in_3), .Q(o2), .clk(in_1), .clr(in_2));
  Register #(.width(32)) register_18 (.D(i6), .en(in_3), .Q(o6), .clk(in_1), .clr(in_2));
  Register #(.width(32)) register_19 (.D(i10), .en(in_3), .Q(o10), .clk(in_1), .clr(in_2));
  Register #(.width(32)) register_20 (.D(i14), .en(in_3), .Q(o14), .clk(in_1), .clr(in_2));
  Register #(.width(32)) register_21 (.D(i18), .en(in_3), .Q(o18), .clk(in_1), .clr(in_2));
  Register #(.width(32)) register_22 (.D(i22), .en(in_3), .Q(o22), .clk(in_1), .clr(in_2));
  Register #(.width(32)) register_23 (.D(i26), .en(in_3), .Q(o26), .clk(in_1), .clr(in_2));
  Register #(.width(32)) register_24 (.D(i30), .en(in_3), .Q(o30), .clk(in_1), .clr(in_2));
  Multiplexer #(.select(5), .width(32)) multiplexer_1 (
    .in0({32{1'b0}}), .in1(o1), .in2(o2), .in3(o3), .in4(o4), .in5(o5), .in6(o6), .in7(o7), .in8(o8),
    .in9(o9), .in10(o10), .in11(o11), .in12(o12), .in13(o13), .in14(o14), .in15(o15), .in16(o16), .in17(o17),
    .in18(o18), .in19(o19), .in20(o20), .in21(o21), .in22(o22), .in23(o23), .in24(o24), .in25(o25),
    .in26(o26), .in27(o27), .in28(o28), .in29(o29), .in30(o30), .in31(o31), .out(out_8), .sel(in_4));  // open: en
  Register #(.width(32)) register_25 (.D(i3), .en(in_3), .Q(o3), .clk(in_1), .clr(in_2));
  Register #(.width(32)) register_26 (.D(i7), .en(in_3), .Q(o7), .clk(in_1), .clr(in_2));
  Register #(.width(32)) register_27 (.D(i11), .en(in_3), .Q(o11), .clk(in_1), .clr(in_2));
  Register #(.width(32)) register_28 (.D(i15), .en(in_3), .Q(o15), .clk(in_1), .clr(in_2));
  Register #(.width(32)) register_29 (.D(i19), .en(in_3), .Q(o19), .clk(in_1), .clr(in_2));
  Register #(.width(32)) register_30 (.D(i23), .en(in_3), .Q(o23), .clk(in_1), .clr(in_2));
  Register #(.width(32)) register_31 (.D(i27), .en(in_3), .Q(o27), .clk(in_1), .clr(in_2));
  Register #(.width(32)) register_32 (.D(i31), .en(in_3), .Q(o31), .clk(in_1), .clr(in_2));
  Multiplexer #(.select(5), .width(32)) multiplexer_2 (
    .in0({32{1'b0}}), .in1(o1), .in2(o2), .in3(o3), .in4(o4), .in5(o5), .in6(o6), .in7(o7), .in8(o8),
    .in9(o9), .in10(o10), .in11(o11), .in12(o12), .in13(o13), .in14(o14), .in15(o15), .in16(o16), .in17(o17),
    .in18(o18), .in19(o19), .in20(o20), .in21(o21), .in22(o22), .in23(o23), .in24(o24), .in25(o25),
    .in26(o26), .in27(o27), .in28(o28), .in29(o29), .in30(o30), .in31(o31), .out(out_9), .sel(in_5));  // open: en

  // Other names for the same wires on the sheet: A1[4:0] = in_4; A2[4:0] = in_5; A3[4:0] = in_6; clk = in_1;
  //   RD1[31:0] = out_8; RD2[31:0] = out_9; reset = in_2; WD[31:0] = in_7; WE = in_3
endmodule

module ALU (
  input  [2:0] in_1,
  input  [31:0] in_2,
  input  [31:0] in_3,
  input  [4:0] in_4,
  output [31:0] ALUOut,
  output GreaterZero,
  output Zero,
  output LessZero
);

  wire [31:0] adder_1_out, and_1_out, not_1_out, or_1_out, or_2_out, shifter_1_out, shifter_2_out,
       shifter_3_out, subtractor_1_out;

  Adder #(.width(32)) adder_1 (.a(in_2), .b(in_3), .out(adder_1_out));  // open: cin, cout
  Subtractor #(.width(32)) subtractor_1 (.a(in_2), .b(in_3), .out(subtractor_1_out));  // open: bin, bout
  assign and_1_out = in_2 & in_3;  // AND_Gate and_1, 32 bits wide
  assign or_1_out = in_2 | in_3;  // OR_Gate or_1, 32 bits wide
  Shifter #(.width(32)) shifter_1 (.in(in_3), .\dist (in_4), .out(shifter_1_out));
  Shifter #(.width(32)) shifter_2 (.in(in_3), .\dist (in_4), .out(shifter_2_out));
  Shifter #(.width(32)) shifter_3 (.in({32{1'b1}}), .\dist (in_4), .out(shifter_3_out));
  assign not_1_out = ~shifter_3_out;  // NOT_Gate not_1, 32 bits wide
  assign or_2_out = shifter_2_out | not_1_out;  // OR_Gate or_2, 32 bits wide
  Multiplexer #(.select(3), .width(32)) multiplexer_1 (
    .in0(adder_1_out), .in1(subtractor_1_out), .in2(and_1_out), .in3(or_1_out), .in4(shifter_1_out),
    .out(ALUOut), .sel(in_1));  // open: in5, in6, in7, en
  Comparator #(.width(32)) comparator_1 (.a(in_2), .b({32{1'b0}}), .gt(GreaterZero));  // open: eq, lt
  Comparator #(.width(32)) comparator_2 (.a(in_2), .b(in_3), .eq(Zero));  // open: gt, lt
  Comparator #(.width(32)) comparator_3 (.a(in_2), .b({32{1'b0}}), .lt(LessZero));  // open: gt, eq

  // Other names for the same wires on the sheet: ALUControl[2:0] = in_1; shamt[4:0] = in_4; SrcA[31:0] = in_2;
  //   SrcB[31:0] = in_3

  // Notes on the sheet:
  //   SLO的一种实践
endmodule

module Controller (
  input  [5:0] opcode,
  input  [5:0] funct,
  output out_3,
  output out_4,
  output [2:0] ALUControl,
  output MemRead,
  output MemWrite,
  output RegWrite,
  output [2:0] Mem2Reg,
  output [1:0] EXTControl,
  output ALUSrc,
  output [1:0] RegDst,
  output [2:0] NPCControl
);

  wire add, addi, j, jalr, jr, lw, not_1_out, not_2_out, not_3_out, not_4_out, not_5_out, not_6_out,
       not_7_out, not_8_out, not_9_out, not_10_out, not_11_out, not_12_out, not_13_out, not_14_out,
       not_15_out, not_16_out, not_17_out, not_18_out, not_19_out, not_20_out, not_21_out, not_22_out,
       not_23_out, not_24_out, not_25_out, not_26_out, not_27_out, R, sub;

  not not_1 (not_1_out, opcode[0]);
  not not_2 (not_2_out, opcode[1]);
  not not_3 (not_3_out, opcode[2]);
  not not_4 (not_4_out, opcode[3]);
  not not_5 (not_5_out, opcode[4]);
  not not_6 (not_6_out, opcode[5]);
  not not_7 (not_7_out, funct[0]);
  not not_8 (not_8_out, funct[1]);
  not not_9 (not_9_out, funct[2]);
  not not_10 (not_10_out, funct[3]);
  not not_11 (not_11_out, funct[4]);
  not not_12 (not_12_out, funct[5]);
  and and_1 (R, not_1_out, not_2_out, not_3_out, not_4_out, not_5_out, not_6_out);
  and and_2 (add, R, not_7_out, not_8_out, not_9_out, not_10_out, not_11_out, funct[5]);
  not not_13 (not_13_out, add);
  and and_3 (sub, R, not_7_out, funct[1], not_9_out, not_10_out, not_11_out, funct[5]);
  not not_14 (not_14_out, sub);
  and and_4 (ALUControl[1], opcode[0], not_2_out, opcode[2], opcode[3], not_5_out, not_6_out);
  not not_15 (not_15_out, ALUControl[1]);
  and and_5 (lw, opcode[0], opcode[1], not_3_out, not_4_out, not_5_out, opcode[5]);
  not not_16 (not_16_out, lw);
  and and_6 (MemWrite, opcode[0], opcode[1], not_3_out, opcode[3], not_5_out, opcode[5]);
  not not_17 (not_17_out, MemWrite);
  and and_7 (out_3, not_1_out, not_2_out, opcode[2], not_4_out, not_5_out, not_6_out);
  not not_18 (not_18_out, out_3);
  and and_8 (EXTControl[1], opcode[0], opcode[1], opcode[2], opcode[3], not_5_out, not_6_out);
  not not_19 (not_19_out, EXTControl[1]);
  and and_9 (j, not_1_out, opcode[1], not_3_out, not_4_out, not_5_out, not_6_out);
  not not_20 (not_20_out, j);
  and and_10 (jr, R, not_7_out, not_8_out, not_9_out, funct[3], not_11_out, not_12_out);
  not not_21 (not_21_out, jr);
  and and_11 (RegDst[1], opcode[0], opcode[1], not_3_out, not_4_out, not_5_out, not_6_out);
  not not_22 (not_22_out, RegDst[1]);
  and and_12 (jalr, R, funct[0], not_8_out, not_9_out, funct[3], not_11_out, not_12_out);
  not not_23 (not_23_out, jalr);
  and and_13 (ALUControl[2], R, not_7_out, not_8_out, not_9_out, not_10_out, not_11_out, not_12_out);
  not not_24 (not_24_out, ALUControl[2]);
  and and_14 (Mem2Reg[2], not_1_out, not_2_out, not_3_out, not_4_out, not_5_out, opcode[5]);
  not not_25 (not_25_out, Mem2Reg[2]);
  and and_15 (addi, not_1_out, not_2_out, not_3_out, opcode[3], not_5_out, not_6_out);
  not not_26 (not_26_out, addi);
  and and_16 (out_4, opcode[0], opcode[1], opcode[2], not_4_out, not_5_out, not_6_out);
  not not_27 (not_27_out, out_4);
  or or_1 (NPCControl[0], out_3, out_4);
  or or_2 (NPCControl[1], j, RegDst[1]);
  or or_3 (NPCControl[2], jr, jalr);
  or or_4 (Mem2Reg[0], lw, RegDst[1], jalr);
  or or_5 (Mem2Reg[1], EXTControl[1], RegDst[1], jalr);
  or or_6 (ALUControl[0], sub, ALUControl[1]);
  or or_7 (MemRead, lw, Mem2Reg[2]);
  or or_8 (EXTControl[0], lw, MemWrite, out_3, Mem2Reg[2], addi, out_4);
  or or_9 (ALUSrc, ALUControl[1], lw, MemWrite, EXTControl[1], Mem2Reg[2], addi);
  or or_10 (RegDst[0], add, sub, jalr, ALUControl[2]);
  or or_11 (RegWrite, add, sub, ALUControl[1], lw, EXTControl[1], RegDst[1], jalr, ALUControl[2], Mem2Reg[2], addi);

  // Other names for the same wires on the sheet: ori = ALUControl[1]; sll = ALUControl[2]; beq = out_3; bgtz = out_4;
  //   lui = EXTControl[1]; lb = Mem2Reg[2]; jal = RegDst[1]; sw = MemWrite
endmodule

module EXT (
  input  [1:0] EXTControl,
  input  [15:0] in_2,
  output [31:0] out_3
);

  wire [31:0] bit_extender_1_out, bit_extender_2_out, bit_extender_3_out, shifter_1_out;

  assign bit_extender_1_out = {{16{1'b0}}, in_2};  // Bit_Extender bit_extender_1
  assign bit_extender_2_out = {{16{in_2[15]}}, in_2};  // Bit_Extender bit_extender_2
  assign bit_extender_3_out = {{16{1'b0}}, in_2};  // Bit_Extender bit_extender_3
  Shifter #(.width(32)) shifter_1 (.in(bit_extender_3_out), .\dist (5'b10000), .out(shifter_1_out));
  Multiplexer #(.select(2), .width(32)) multiplexer_1 (
    .in0(bit_extender_1_out), .in1(bit_extender_2_out), .in2(shifter_1_out), .out(out_3), .sel(EXTControl));  // open: in3, en
endmodule

module DM (
  input  in_1,
  input  in_2,
  input  in_3,
  input  in_4,
  input  [31:0] A,
  input  [31:0] WD,
  output [31:0] out_7
);

  wire [11:0] bit_extender_1_out;
  wire [31:0] shifter_1_out;

  Shifter #(.width(32), .shift("lr")) shifter_1 (.in(A), .\dist (5'b00010), .out(shifter_1_out));
  Bit_Extender #(.in_width(32), .out_width(12)) bit_extender_1 (.in(shifter_1_out), .out(bit_extender_1_out));
  RAM #(.addrWidth(12), .dataWidth(32), .bus("separate")) ram_1 (
    .addr(bit_extender_1_out), .din(WD), .data(out_7), .str(in_3), .clk(in_1), .ld(in_4), .clr(in_2));  // open: sel

  // Other names for the same wires on the sheet: clk = in_1; MemRead = in_4; MemWrite = in_3; reset = in_2
endmodule

module Splitter (
  input  [31:0] Instr,
  output [5:0] opcode,
  output [4:0] rs,
  output [4:0] rt,
  output [4:0] rd,
  output [4:0] shamt,
  output [5:0] funct,
  output [15:0] Imm16,
  output [25:0] Imm26
);

  Bit_Extender #(.in_width(32)) bit_extender_1 (.in(Instr), .out(Imm16));
  Bit_Extender #(.in_width(32), .out_width(26)) bit_extender_2 (.in(Instr), .out(Imm26));

  assign funct = Instr[5:0];
  assign opcode = Instr[31:26];
  assign rd = Instr[15:11];
  assign rs = Instr[25:21];
  assign rt = Instr[20:16];
  assign shamt = Instr[10:6];
endmodule

module test (
  input  [31:0] in_1,
  output [31:0] out_2,
  output [31:0] out_3,
  output [4:0] out_4,
  output [1:0] out_5
);

  Adder #(.width(32)) adder_1 (.a({32{1'b1}}), .b({32{1'b1}}), .out(out_2));  // open: cin, cout
  Subtractor #(.width(32)) subtractor_1 (.a(32'h7cf), .b(32'hfbd), .out(out_3));  // open: bin, bout

  assign out_4 = in_1[6:2];
  assign out_5 = in_1[1:0];
endmodule
