// Logisim project tetris.circ as structural Verilog: 3 circuits, main circuit main
module main (
  input  [7:0] in_1,
  input  in_2,
  input  in_3,
  output [1:0] out_4
);

  wire [7:0] register_1_q, statetrans_1_out_3;

  StateTrans statetrans_1 (.in_1(register_1_q), .in_2(in_1), .out_3(statetrans_1_out_3));
  // Probe on statetrans_1_out_3
  Register register_1 (.D(statetrans_1_out_3), .Q(register_1_q), .clk(in_3), .clr(in_2));  // open: en
  // Probe on register_1_q
  Output output_1 (.in_1(register_1_q), .in_2(in_1), .out_3(out_4));

  // Other names for the same wires on the sheet: clk = in_3; input[7:0] = in_1; reset = in_2
endmodule

module StateTrans (
  input  [7:0] in_1,
  input  [7:0] in_2,
  output [7:0] out_3
);

  wire block, comparator_1_eq, full, normal;
  wire [7:0] and_1_out, multiplexer_1_out, next;

  Multiplexer #(.width(8)) multiplexer_1 (
    .in0(next), .in1({8{1'b0}}), .out(multiplexer_1_out), .sel(full));  // open: en
  assign and_1_out = in_1 & in_2;  // AND_Gate and_1, 8 bits wide
  assign next = in_1 | in_2;  // OR_Gate or_1, 8 bits wide
  Multiplexer #(.width(8)) multiplexer_2 (.in0(multiplexer_1_out), .in1(in_2), .out(out_3), .sel(block));  // open: en
  Comparator comparator_1 (.a({8{1'b0}}), .b(and_1_out), .eq(comparator_1_eq));  // open: gt, lt
  Comparator comparator_2 (.a({8{1'b1}}), .b(next), .eq(full));  // open: gt, lt
  not not_1 (block, comparator_1_eq);
  not not_2 (normal, full);

  // Other names for the same wires on the sheet: input[7:0] = in_1; state[7:0] = in_2
endmodule

module Output (
  input  [7:0] in_1,
  input  [7:0] in_2,
  output [1:0] out_3
);

  wire block, comparator_1_eq, full, normal;
  wire [1:0] multiplexer_1_out;
  wire [7:0] and_1_out, next;

  Multiplexer #(.width(2)) multiplexer_1 (.in0(2'b10), .in1(2'b11), .out(multiplexer_1_out), .sel(full));  // open: en
  assign and_1_out = in_1 & in_2;  // AND_Gate and_1, 8 bits wide
  assign next = in_1 | in_2;  // OR_Gate or_1, 8 bits wide
  Multiplexer #(.width(2)) multiplexer_2 (.in0(multiplexer_1_out), .in1(2'b01), .out(out_3), .sel(block));  // open: en
  Comparator comparator_1 (.a({8{1'b0}}), .b(and_1_out), .eq(comparator_1_eq));  // open: gt, lt
  Comparator comparator_2 (.a({8{1'b1}}), .b(next), .eq(full));  // open: gt, lt
  not not_1 (block, comparator_1_eq);
  not not_2 (normal, full);

  // Other names for the same wires on the sheet: input[7:0] = in_1; state[7:0] = in_2
endmodule
