// Logisim project fib.circ as structural Verilog: 3 circuits, main circuit main
module main (
  input  [2:0] in_1,
  output [3:0] out_2
);

  wire clk, comparator_1_lt, counter_1_q, enable;
  wire [3:0] adder_1_out, bit_extender_1_out, counter_2_q, multiplexer_1_out, now, prev;

  Clock clock_1 (.out(clk));
  Counter #(.width(1), .max('h1), .ongoal("stay")) counter_1 (
    .Q(counter_1_q), .clk(clk));  // open: load, D, count, carry, clr
  assign bit_extender_1_out = {{1{1'b0}}, in_1};  // Bit_Extender bit_extender_1
  Counter #(.width(4), .max('hf), .ongoal("stay")) counter_2 (
    .Q(counter_2_q), .clk(clk));  // open: load, D, count, carry, clr
  Multiplexer #(.width(4)) multiplexer_1 (
    .in0(4'b0001), .in1(now), .out(multiplexer_1_out), .sel(counter_1_q));  // open: en
  Adder #(.width(4)) adder_1 (.a(now), .b(prev), .out(adder_1_out));  // open: cin, cout
  Comparator #(.width(4), .mode("unsigned")) comparator_1 (
    .a(bit_extender_1_out), .b(counter_2_q), .lt(comparator_1_lt));  // open: gt, eq
  Register #(.width(4)) register_1 (.D(multiplexer_1_out), .en(enable), .Q(prev), .clk(clk));  // open: clr
  Register #(.width(4)) register_2 (.D(adder_1_out), .en(enable), .Q(now), .clk(clk));  // open: clr
  not not_1 (enable, comparator_1_lt);
  Multiplexer #(.width(4)) multiplexer_2 (.in0(4'b0000), .in1(now), .out(out_2), .sel(comparator_1_lt));  // open: en
endmodule

module counting (
  input  [2:0] in_1,
  output out_2
);

  wire [3:0] bit_extender_1_out, undriven;

  Clock clock_1 ();  // open: out
  assign bit_extender_1_out = {{1{1'b0}}, in_1};  // Bit_Extender bit_extender_1
  Comparator #(.width(4)) comparator_1 (.a(bit_extender_1_out), .b(undriven), .lt(out_2));  // open: gt, eq
endmodule

module calculating (
  input  in_1,
  output [3:0] out_2
);

  wire clk, counter_1_q, enable;
  wire [3:0] adder_1_out, multiplexer_1_out, prev;

  Clock clock_1 (.out(clk));
  not not_1 (enable, in_1);
  Counter #(.width(1), .max('h1)) counter_1 (.Q(counter_1_q), .clk(clk));  // open: load, D, count, carry, clr
  Register #(.width(4)) register_1 (.D(multiplexer_1_out), .en(enable), .Q(prev), .clk(clk));  // open: clr
  Multiplexer #(.width(4)) multiplexer_1 (
    .in0(4'b0001), .in1(out_2), .out(multiplexer_1_out), .sel(counter_1_q));  // open: en
  Register #(.width(4)) register_2 (.D(adder_1_out), .en(enable), .Q(out_2), .clk(clk));  // open: clr
  Adder #(.width(4)) adder_1 (.a(out_2), .b(prev), .out(adder_1_out));  // open: cin, cout

  // Other names for the same wires on the sheet: now[3:0] = out_2
endmodule
