// Logisim project sort.circ as structural Verilog: 4 circuits, main circuit 1bit_swap
module _1bit_swap (
  input  I1,
  input  I2,
  input  S,
  output O1,
  output O2
);

  wire and_1_out, and_2_out, and_3_out, and_4_out, not_1_out;

  not not_1 (not_1_out, S);
  and and_1 (and_1_out, not_1_out, I1);
  and and_2 (and_2_out, S, I2);
  and and_3 (and_3_out, not_1_out, I2);
  and and_4 (and_4_out, S, I1);
  or or_1 (O1, and_1_out, and_2_out);
  or or_2 (O2, and_3_out, and_4_out);
endmodule

module _4bit_swap (
  input  [3:0] in_1,
  input  [3:0] in_2,
  input  enable,
  output [3:0] out_4,
  output [3:0] out_5
);

  _1bit_swap u_1bit_swap_1 (.I1(in_1[0]), .I2(in_2[0]), .S(enable), .O1(out_4[0]), .O2(out_5[0]));
  _1bit_swap u_1bit_swap_2 (.I1(in_1[1]), .I2(in_2[1]), .S(enable), .O1(out_4[1]), .O2(out_5[1]));
  _1bit_swap u_1bit_swap_3 (.I1(in_1[2]), .I2(in_2[2]), .S(enable), .O1(out_4[2]), .O2(out_5[2]));
  _1bit_swap u_1bit_swap_4 (.I1(in_1[3]), .I2(in_2[3]), .S(enable), .O1(out_4[3]), .O2(out_5[3]));
endmodule

module swap (
  input  [3:0] Input1,
  input  [3:0] Input2,
  input  [3:0] Input3,
  input  [3:0] Input4,
  output [3:0] Output1,
  output [3:0] Output2,
  output [3:0] Output3,
  output [3:0] Output4
);

  wire comparator_1_gt, comparator_2_gt, comparator_3_gt;
  wire [3:0] n4bit_swap_1_out_5, n4bit_swap_2_out_5;

  Comparator #(.width(4), .mode("unsigned")) comparator_1 (
    .a(Input1), .b(Input2), .gt(comparator_1_gt));  // open: eq, lt
  Comparator #(.width(4), .mode("unsigned")) comparator_2 (
    .a(n4bit_swap_1_out_5), .b(Input3), .gt(comparator_2_gt));  // open: eq, lt
  Comparator #(.width(4), .mode("unsigned")) comparator_3 (
    .a(n4bit_swap_2_out_5), .b(Input4), .gt(comparator_3_gt));  // open: eq, lt
  _4bit_swap u_4bit_swap_1 (
    .in_1(Input1), .in_2(Input2), .enable(comparator_1_gt), .out_4(Output1), .out_5(n4bit_swap_1_out_5));
  _4bit_swap u_4bit_swap_2 (
    .in_1(n4bit_swap_1_out_5), .in_2(Input3), .enable(comparator_2_gt), .out_4(Output2),
    .out_5(n4bit_swap_2_out_5));
  _4bit_swap u_4bit_swap_3 (
    .in_1(n4bit_swap_2_out_5), .in_2(Input4), .enable(comparator_3_gt), .out_4(Output3), .out_5(Output4));
endmodule

module _4bit_sort (
  input  [3:0] in_1,
  input  [3:0] in_2,
  input  [3:0] in_3,
  input  [3:0] in_4,
  output [3:0] out_5,
  output [3:0] out_6,
  output [3:0] out_7,
  output [3:0] out_8
);

  wire [3:0] swap_1_output1, swap_1_output2, swap_1_output3, swap_1_output4, swap_2_output1, swap_2_output2,
       swap_2_output3, swap_2_output4, swap_3_output1, swap_3_output2, swap_3_output3, swap_3_output4,
       swap_4_output1, swap_4_output2, swap_4_output3, swap_4_output4, swap_5_output1, swap_5_output2,
       swap_5_output3, swap_5_output4;

  swap swap_1 (
    .Input1(in_1), .Input2(in_2), .Input3(in_3), .Input4(in_4), .Output1(swap_1_output1),
    .Output2(swap_1_output2), .Output3(swap_1_output3), .Output4(swap_1_output4));
  swap swap_2 (
    .Input1(swap_1_output1), .Input2(swap_1_output2), .Input3(swap_1_output3), .Input4(swap_1_output4),
    .Output1(swap_2_output1), .Output2(swap_2_output2), .Output3(swap_2_output3), .Output4(swap_2_output4));
  swap swap_3 (
    .Input1(swap_2_output1), .Input2(swap_2_output2), .Input3(swap_2_output3), .Input4(swap_2_output4),
    .Output1(swap_3_output1), .Output2(swap_3_output2), .Output3(swap_3_output3), .Output4(swap_3_output4));
  swap swap_4 (
    .Input1(swap_5_output1), .Input2(swap_5_output2), .Input3(swap_5_output3), .Input4(swap_5_output4),
    .Output1(swap_4_output1), .Output2(swap_4_output2), .Output3(swap_4_output3), .Output4(swap_4_output4));
  swap swap_5 (
    .Input1(swap_3_output1), .Input2(swap_3_output2), .Input3(swap_3_output3), .Input4(swap_3_output4),
    .Output1(swap_5_output1), .Output2(swap_5_output2), .Output3(swap_5_output3), .Output4(swap_5_output4));
  swap swap_6 (
    .Input1(swap_4_output1), .Input2(swap_4_output2), .Input3(swap_4_output3), .Input4(swap_4_output4),
    .Output1(out_5), .Output2(out_6), .Output3(out_7), .Output4(out_8));
endmodule
