// Logisim project swap.circ as structural Verilog: 1 circuit, main circuit swap
module swap (
  input  a,
  input  b,
  input  c,
  output x,
  output y
);

  wire nand_1_out, nand_2_out, nand_3_out, nand_4_out, nand_5_out, nand_6_out;

  nand nand_1 (nand_1_out, c, c);
  nand nand_2 (nand_2_out, c, c);
  nand nand_3 (nand_3_out, b, c);
  nand nand_4 (nand_4_out, a, nand_1_out);
  nand nand_5 (nand_5_out, b, nand_2_out);
  nand nand_6 (nand_6_out, a, c);
  nand nand_7 (x, nand_3_out, nand_4_out);
  nand nand_8 (y, nand_5_out, nand_6_out);
endmodule
