// Logisim project mod51.circ as structural Verilog: 4 circuits, main circuit mod5
module mod5 (
  input  in_1,
  output out_2,
  output out_3,
  output out_4,
  output out_5,
  output out_6
);

  wire \状态存储_1_o1 , \状态存储_1_o2 , \状态转移_1_o1 , \状态转移_1_o2 ;

  \状态转移  \u_状态转移_1  (.S0(\状态存储_1_o2 ), .S1(\状态存储_1_o1 ), .In(in_1), .O1(\状态转移_1_o1 ), .O2(\状态转移_1_o2 ));
  \状态存储  \u_状态存储_1  (.In1(\状态转移_1_o1 ), .In2(\状态转移_1_o2 ), .O1(\状态存储_1_o1 ), .O2(\状态存储_1_o2 ));
  \输出  \u_输出_1  (
    .S1(\状态存储_1_o1 ), .S0(\状态存储_1_o2 ), .In(in_1), .O0(out_2), .O1(out_3), .O2(out_4), .O3(out_5), .O4(out_6));
endmodule

module \状态转移  (
  input  S0,
  input  S1,
  input  In,
  output O1,
  output O2
);

  wire and_1_out, and_2_out, and_3_out, and_4_out, and_5_out, and_6_out, and_7_out, and_8_out, and_9_out,
       and_10_out, not_1_out, not_2_out, not_3_out, not_4_out, not_5_out, not_6_out, not_7_out, not_8_out,
       or_2_out, or_3_out;

  not not_1 (not_1_out, S0);
  not not_2 (not_2_out, S1);
  not not_3 (not_3_out, S0);
  not not_4 (not_4_out, S1);
  not not_5 (not_5_out, S0);
  not not_6 (not_6_out, S1);
  and and_1 (and_1_out, not_1_out, S1);
  and and_2 (and_2_out, S0, not_2_out);
  and and_3 (and_3_out, not_3_out, not_4_out);
  and and_4 (and_4_out, not_5_out, S1);
  not not_7 (not_7_out, In);
  and and_5 (and_5_out, S0, not_6_out);
  not not_8 (not_8_out, In);
  and and_6 (and_6_out, S0, S1);
  or or_1 (O1, and_1_out, and_2_out);
  and and_7 (and_7_out, and_3_out, In);
  and and_8 (and_8_out, and_4_out, not_7_out);
  and and_9 (and_9_out, and_5_out, not_8_out);
  and and_10 (and_10_out, and_6_out, In);
  or or_2 (or_2_out, and_7_out, and_8_out);
  or or_3 (or_3_out, and_9_out, and_10_out);
  or or_4 (O2, or_2_out, or_3_out);
endmodule

module \状态存储  (
  input  In1,
  input  In2,
  output O1,
  output O2
);

  wire clock_1_out;

  Clock clock_1 (.out(clock_1_out));
  Register #(.width(1)) register_1 (.D(In1), .Q(O1), .clk(clock_1_out));  // open: en, clr
  Register #(.width(1)) register_2 (.D(In2), .Q(O2), .clk(clock_1_out));  // open: en, clr
endmodule

module \输出  (
  input  S1,
  input  S0,
  input  In,
  output O0,
  output O1,
  output O2,
  output O3,
  output O4
);

  wire and_1_out, and_2_out, and_3_out, and_4_out, and_5_out, and_6_out, and_7_out, and_8_out, and_9_out,
       and_10_out, and_11_out, and_12_out, and_13_out, and_14_out, and_15_out, and_16_out, not_1_out,
       not_2_out, not_3_out, not_4_out, not_5_out, not_6_out, not_7_out, not_8_out, not_9_out, not_10_out,
       not_11_out, not_12_out;

  not not_1 (not_1_out, S1);
  not not_2 (not_2_out, S0);
  not not_3 (not_3_out, S1);
  not not_4 (not_4_out, S0);
  not not_5 (not_5_out, S1);
  not not_6 (not_6_out, S0);
  not not_7 (not_7_out, S1);
  not not_8 (not_8_out, S0);
  and and_1 (and_1_out, not_1_out, not_2_out);
  not not_9 (not_9_out, In);
  and and_2 (and_2_out, S1, S0);
  not not_10 (not_10_out, In);
  and and_3 (and_3_out, not_3_out, not_4_out);
  and and_4 (and_4_out, S1, S0);
  and and_5 (and_5_out, not_5_out, S0);
  and and_6 (and_6_out, S1, not_6_out);
  and and_7 (and_7_out, not_7_out, S0);
  not not_11 (not_11_out, In);
  and and_8 (and_8_out, S1, not_8_out);
  not not_12 (not_12_out, In);
  and and_9 (and_9_out, and_1_out, not_9_out);
  and and_10 (and_10_out, and_2_out, not_10_out);
  and and_11 (and_11_out, and_3_out, In);
  and and_12 (and_12_out, and_4_out, In);
  and and_13 (and_13_out, and_5_out, In);
  and and_14 (and_14_out, and_6_out, In);
  and and_15 (and_15_out, and_7_out, not_11_out);
  and and_16 (and_16_out, and_8_out, not_12_out);
  or or_1 (O1, and_9_out, and_10_out);
  or or_2 (O2, and_11_out, and_12_out);
  or or_3 (O3, and_13_out, and_14_out);
  or or_4 (O4, and_15_out, and_16_out);

  assign O0 = 1'b0;
endmodule
