// Logisim project div.circ as structural Verilog: 1 circuit, main circuit main
module main (
  input  [8:0] in_1,
  input  [1:0] in_2,
  output [3:0] out_3,
  output [3:0] out_4,
  output [3:0] out_5
);

  wire [3:0] Hi, Hi0, Hi2, Low, Low0, Mid, Mid0;
  wire [8:0] divider_1_out, divider_1_rem, divider_2_out, divider_2_rem, divider_3_rem;

  assign Hi0 = {{1{1'b0}}, in_1[8:6]};  // Bit_Extender bit_extender_1
  assign Mid0 = {{1{1'b0}}, in_1[5:3]};  // Bit_Extender bit_extender_2
  assign Low0 = {{1{1'b0}}, in_1[2:0]};  // Bit_Extender bit_extender_3
  assign Hi2 = {{3{1'b0}}, in_1[8]};  // Bit_Extender bit_extender_4
  Divider #(.width(9)) divider_1 (.a(in_1), .b(9'ha), .out(divider_1_out), .rem(divider_1_rem));  // open: upper
  Bit_Extender #(.in_width(9), .out_width(4)) bit_extender_5 (.in(divider_1_rem), .out(Low));
  Divider #(.width(9)) divider_2 (
    .a(divider_1_out), .b(9'ha), .out(divider_2_out), .rem(divider_2_rem));  // open: upper
  Bit_Extender #(.in_width(9), .out_width(4)) bit_extender_6 (.in(divider_2_rem), .out(Mid));
  Divider #(.width(9)) divider_3 (.a(divider_2_out), .b(9'ha), .rem(divider_3_rem));  // open: out, upper
  Bit_Extender #(.in_width(9), .out_width(4)) bit_extender_7 (.in(divider_3_rem), .out(Hi));
  Multiplexer #(.select(2), .width(4)) multiplexer_1 (
    .in0(Hi0), .in1(Hi), .in2(Hi2), .out(out_3), .sel(in_2));  // open: in3, en
  Multiplexer #(.select(2), .width(4)) multiplexer_2 (
    .in0(Mid0), .in1(Mid), .in2(in_1[7:4]), .out(out_4), .sel(in_2));  // open: in3, en
  Multiplexer #(.select(2), .width(4)) multiplexer_3 (
    .in0(Low0), .in1(Low), .in2(in_1[3:0]), .out(out_5), .sel(in_2));  // open: in3, en

  // Other names for the same wires on the sheet: Input[8:0] = in_1; Low2[3:0] = in_1[3:0]; Mid2[3:0] = in_1[7:4];
  //   Sel[1:0] = in_2
endmodule
