// Logisim project mod_5.circ as structural Verilog: 3 circuits, main circuit mod5
module mod5 (
  input  in_1,
  output out_2,
  output out_3,
  output out_4,
  output out_5,
  output out_6
);

  wire Clock, register_1_q, register_2_q, statetransformation_1_c02, statetransformation_1_c12;

  Clock clock_1 (.out(Clock));
  StateTransformation statetransformation_1 (
    .C1(register_2_q), .C0(register_1_q), .B(in_1), .C12(statetransformation_1_c12),
    .C02(statetransformation_1_c02));
  Register #(.width(1)) register_1 (.D(statetransformation_1_c12), .Q(register_1_q), .clk(Clock));  // open: en, clr
  Register #(.width(1)) register_2 (.D(statetransformation_1_c02), .Q(register_2_q), .clk(Clock));  // open: en, clr
  stateOutput stateoutput_1 (
    .C1(register_1_q), .C0(register_2_q), .B(in_1), .S0(out_2), .S1(out_3), .S2(out_4), .S3(out_5), .S4(out_6));
endmodule

module StateTransformation (
  input  C1,
  input  C0,
  input  B,
  output C12,
  output C02
);

  wire and_1_out, and_2_out, and_3_out, and_4_out, and_5_out, and_6_out, and_7_out, and_8_out, and_9_out,
       and_10_out, not_1_out, not_2_out, not_3_out, not_4_out, not_5_out, not_6_out, not_7_out, not_8_out,
       or_2_out, or_3_out;

  not not_1 (not_1_out, C1);
  not not_2 (not_2_out, C0);
  not not_3 (not_3_out, C1);
  not not_4 (not_4_out, C0);
  not not_5 (not_5_out, C1);
  not not_6 (not_6_out, C0);
  and and_1 (and_1_out, not_1_out, C0);
  and and_2 (and_2_out, C1, not_2_out);
  and and_3 (and_3_out, not_3_out, not_4_out);
  and and_4 (and_4_out, not_5_out, C0);
  not not_7 (not_7_out, B);
  and and_5 (and_5_out, C1, not_6_out);
  not not_8 (not_8_out, B);
  and and_6 (and_6_out, C1, C0);
  or or_1 (C12, and_1_out, and_2_out);
  and and_7 (and_7_out, and_3_out, B);
  and and_8 (and_8_out, and_4_out, not_7_out);
  and and_9 (and_9_out, and_5_out, not_8_out);
  and and_10 (and_10_out, and_6_out, B);
  or or_2 (or_2_out, and_7_out, and_8_out);
  or or_3 (or_3_out, and_9_out, and_10_out);
  or or_4 (C02, or_2_out, or_3_out);
endmodule

module stateOutput (
  input  C1,
  input  C0,
  input  B,
  output S0,
  output S1,
  output S2,
  output S3,
  output S4
);

  wire and_1_out, and_2_out, and_3_out, and_4_out, and_5_out, and_6_out, and_7_out, and_8_out, and_9_out,
       and_10_out, and_11_out, and_12_out, and_13_out, and_14_out, and_15_out, and_16_out, not_1_out,
       not_2_out, not_3_out, not_4_out, not_5_out, not_6_out, not_7_out, not_8_out, not_9_out, not_10_out,
       not_11_out, not_12_out;

  not not_1 (not_1_out, C1);
  not not_2 (not_2_out, C0);
  not not_3 (not_3_out, C1);
  not not_4 (not_4_out, C0);
  not not_5 (not_5_out, C1);
  not not_6 (not_6_out, C0);
  not not_7 (not_7_out, C1);
  not not_8 (not_8_out, C0);
  and and_1 (and_1_out, not_1_out, not_2_out);
  not not_9 (not_9_out, B);
  and and_2 (and_2_out, C1, C0);
  not not_10 (not_10_out, B);
  and and_3 (and_3_out, not_3_out, not_4_out);
  and and_4 (and_4_out, C1, C0);
  and and_5 (and_5_out, not_5_out, C0);
  and and_6 (and_6_out, C1, not_6_out);
  and and_7 (and_7_out, not_7_out, C0);
  not not_11 (not_11_out, B);
  and and_8 (and_8_out, C1, not_8_out);
  not not_12 (not_12_out, B);
  and and_9 (and_9_out, and_1_out, not_9_out);
  and and_10 (and_10_out, and_2_out, not_10_out);
  and and_11 (and_11_out, and_3_out, B);
  and and_12 (and_12_out, and_4_out, B);
  and and_13 (and_13_out, and_5_out, B);
  and and_14 (and_14_out, and_6_out, B);
  and and_15 (and_15_out, and_7_out, not_11_out);
  and and_16 (and_16_out, and_8_out, not_12_out);
  or or_1 (S1, and_9_out, and_10_out);
  or or_2 (S2, and_11_out, and_12_out);
  or or_3 (S3, and_13_out, and_14_out);
  or or_4 (S4, and_15_out, and_16_out);

  assign S0 = 1'b0;
endmodule
