// Logisim project mod5.circ as structural Verilog: 4 circuits, main circuit mod5
module mod5 (
  input  in_1,
  output out_2,
  output out_3,
  output out_4,
  output out_5,
  output out_6
);

  wire reg_1_out_3, reg_1_out_4, trans_1_x, trans_1_y;

  trans trans_1 (.a(reg_1_out_3), .b(reg_1_out_4), .c(in_1), .x(trans_1_x), .y(trans_1_y));
  \reg  reg_1 (.in_1(trans_1_x), .in_2(trans_1_y), .out_3(reg_1_out_3), .out_4(reg_1_out_4));
  \output  output_1 (.a(reg_1_out_3), .b(reg_1_out_4), .c(in_1), .x(out_2), .y(out_3), .z(out_4), .u(out_5), .v(out_6));
endmodule

module trans (
  input  a,
  input  b,
  input  c,
  output x,
  output y
);

  wire and_1_out, and_2_out, and_3_out, and_4_out, and_5_out, and_6_out, not_1_out, not_2_out, not_3_out,
       not_4_out, not_5_out, not_6_out, not_7_out, not_8_out;

  not not_1 (not_1_out, a);
  not not_2 (not_2_out, b);
  not not_3 (not_3_out, a);
  not not_4 (not_4_out, b);
  not not_5 (not_5_out, a);
  not not_6 (not_6_out, c);
  not not_7 (not_7_out, b);
  not not_8 (not_8_out, c);
  and and_1 (and_1_out, not_1_out, b);
  and and_2 (and_2_out, a, not_2_out);
  and and_3 (and_3_out, not_3_out, not_4_out, c);
  and and_4 (and_4_out, not_5_out, b, not_6_out);
  and and_5 (and_5_out, a, not_7_out, not_8_out);
  and and_6 (and_6_out, a, b, c);
  or or_1 (x, and_1_out, and_2_out);
  or or_2 (y, and_3_out, and_4_out, and_5_out, and_6_out);
endmodule

module \output  (
  input  a,
  input  b,
  input  c,
  output x,
  output y,
  output z,
  output u,
  output v
);

  wire and_1_out, and_2_out, and_3_out, and_4_out, and_5_out, and_6_out, and_7_out, and_8_out, not_1_out,
       not_2_out, not_3_out, not_4_out, not_5_out, not_6_out, not_7_out, not_8_out, not_9_out, not_10_out,
       not_11_out, not_12_out;

  not not_1 (not_1_out, a);
  not not_2 (not_2_out, b);
  not not_3 (not_3_out, c);
  not not_4 (not_4_out, c);
  not not_5 (not_5_out, a);
  not not_6 (not_6_out, b);
  not not_7 (not_7_out, a);
  not not_8 (not_8_out, b);
  not not_9 (not_9_out, a);
  not not_10 (not_10_out, c);
  not not_11 (not_11_out, b);
  not not_12 (not_12_out, c);
  and and_1 (and_1_out, not_1_out, not_2_out, not_3_out);
  and and_2 (and_2_out, a, b, not_4_out);
  and and_3 (and_3_out, not_5_out, not_6_out, c);
  and and_4 (and_4_out, a, b, c);
  and and_5 (and_5_out, not_7_out, b, c);
  and and_6 (and_6_out, a, not_8_out, c);
  and and_7 (and_7_out, not_9_out, b, not_10_out);
  and and_8 (and_8_out, a, not_11_out, not_12_out);
  or or_1 (y, and_1_out, and_2_out);
  or or_2 (z, and_3_out, and_4_out);
  or or_3 (u, and_5_out, and_6_out);
  or or_4 (v, and_7_out, and_8_out);

  assign x = 1'b0;
endmodule

module \reg  (
  input  in_1,
  input  in_2,
  output out_3,
  output out_4
);

  wire clock_1_out;

  Register #(.width(1)) register_1 (.D(in_1), .Q(out_3), .clk(clock_1_out));  // open: en, clr
  Register #(.width(1)) register_2 (.D(in_2), .Q(out_4), .clk(clock_1_out));  // open: en, clr
  Clock clock_1 (.out(clock_1_out));
endmodule
