// Logisim project swap_mux.circ as structural Verilog: 1 circuit, main circuit swap
module swap (
  input  in_1,
  input  in_2,
  input  in_3,
  output out_4,
  output out_5
);

  wire xor_1_out, xor_2_out, xor_3_out;

  xor xor_1 (xor_1_out, in_1, in_2);
  xor xor_2 (xor_2_out, in_1, xor_1_out);
  xor xor_3 (xor_3_out, in_2, xor_1_out);
  Multiplexer multiplexer_1 (.in0(in_1), .in1(xor_2_out), .out(out_4), .sel(in_3));  // open: en
  Multiplexer multiplexer_2 (.in0(in_2), .in1(xor_3_out), .out(out_5), .sel(in_3));  // open: en

  // Other names for the same wires on the sheet: s = in_3
endmodule
